// Logisim project ALU.circ as structural Verilog: 6 circuits, main circuit main
module main (
  input  AInvert,
  input  Bnegate,
  input  [1:0] OPR,
  input  [31:0] A,
  input  [31:0] B,
  output OV_FLAG,
  output out_7,
  output out_8,
  output out_9,
  output Set_Flag,
  output out_11,
  output out_12,
  output out_13,
  output [3:0] S,
  output [3:0] out_15,
  output [3:0] out_16,
  output [3:0] out_17,
  output Cout,
  output out_19,
  output out_20,
  output out_21,
  output Pg,
  output out_23,
  output out_24,
  output out_25,
  output Gg,
  output out_27,
  output out_28,
  output out_29,
  output c32,
  output out_31,
  output out_32,
  output [31:0] Result,
  output out_34,
  output out_35,
  output out_36,
  output out_37,
  output out_38,
  output out_39,
  output out_40,
  output out_41,
  output out_42,
  output out_43,
  output [3:0] out_44,
  output [3:0] out_45,
  output [3:0] out_46,
  output [3:0] out_47,
  output out_48,
  output out_49,
  output out_50,
  output out_51,
  output out_52,
  output out_53,
  output out_54,
  output out_55,
  output out_56,
  output out_57,
  output out_58,
  output out_59
);

  wire alu_4bit_1_set, alu_4bit_2_set, alu_4bit_3_set, alu_4bit_4_set, alu_4bit_5_set, alu_4bit_6_set,
       alu_4bit_7_set, cla_1_c1, cla_1_c2, cla_1_c3, cla_2_c1, cla_2_c2, cla_2_c3, cla_2_cout, undriven;

  ALU_4BIT alu_4bit_1 (
    .A3(A[31]), .A2(A[30]), .A1(A[29]), .A0(A[28]), .B3(B[31]), .B2(B[30]), .B1(B[29]), .B0(B[28]),
    .AInv(AInvert), .BInv(Bnegate), .C0(cla_1_c3), .Less(1'b0), .OPR(OPR), .OV_FLAG(OV_FLAG),
    .Set_Flag(Set_Flag), .S3(Result[31]), .S2(Result[30]), .S1(Result[29]), .S0(Result[28]),
    .Set(alu_4bit_1_set), .c4(Cout), .Pg(Pg), .Gg(Gg));
  ALU_4BIT alu_4bit_2 (
    .A3(A[15]), .A2(A[14]), .A1(A[13]), .A0(A[12]), .B3(B[15]), .B2(B[14]), .B1(B[13]), .B0(B[12]),
    .AInv(AInvert), .BInv(Bnegate), .C0(cla_2_c3), .Less(1'b0), .OPR(OPR), .OV_FLAG(out_36),
    .Set_Flag(out_40), .S3(out_44[3]), .S2(out_44[2]), .S1(out_44[1]), .S0(out_44[0]), .Set(alu_4bit_2_set),
    .c4(out_48), .Pg(out_52), .Gg(out_56));
  ALU_4BIT alu_4bit_3 (
    .A3(A[27]), .A2(A[26]), .A1(A[25]), .A0(A[24]), .B3(B[27]), .B2(B[26]), .B1(B[25]), .B0(B[24]),
    .AInv(AInvert), .BInv(Bnegate), .C0(cla_1_c2), .Less(1'b0), .OPR(OPR), .OV_FLAG(out_7),
    .Set_Flag(out_11), .S3(out_15[3]), .S2(out_15[2]), .S1(out_15[1]), .S0(out_15[0]), .Set(alu_4bit_3_set),
    .c4(out_19), .Pg(out_23), .Gg(out_27));
  ALU_4BIT alu_4bit_4 (
    .A3(A[11]), .A2(A[10]), .A1(A[9]), .A0(A[8]), .B3(B[11]), .B2(B[10]), .B1(B[9]), .B0(B[8]),
    .AInv(AInvert), .BInv(Bnegate), .C0(cla_2_c2), .Less(1'b0), .OPR(OPR), .OV_FLAG(out_37),
    .Set_Flag(out_41), .S3(out_45[3]), .S2(out_45[2]), .S1(out_45[1]), .S0(out_45[0]), .Set(alu_4bit_4_set),
    .c4(out_49), .Pg(out_53), .Gg(out_57));
  CLA cla_1 (
    .G0(out_29), .C0(Bnegate), .G1(out_28), .G2(out_27), .G3(Gg), .P0(out_25), .P1(out_24), .P2(out_23),
    .P3(Pg), .C3(cla_1_c3), .C1(cla_1_c1), .Cout(c32), .C2(cla_1_c2), .Pg(out_31), .Gg(out_32));
  CLA cla_2 (
    .G0(out_59), .C0(Bnegate), .G1(out_58), .G2(out_57), .G3(out_56), .P0(out_55), .P1(out_54), .P2(out_53),
    .P3(out_52), .C3(cla_2_c3), .C1(cla_2_c1), .Cout(cla_2_cout), .C2(cla_2_c2), .Pg(out_34), .Gg(out_35));
  ALU_4BIT alu_4bit_5 (
    .A3(A[23]), .A2(A[22]), .A1(A[21]), .A0(A[20]), .B3(B[23]), .B2(B[22]), .B1(B[21]), .B0(B[20]),
    .AInv(AInvert), .BInv(Bnegate), .C0(cla_1_c1), .Less(1'b0), .OPR(OPR), .OV_FLAG(out_8),
    .Set_Flag(out_12), .S3(out_16[3]), .S2(out_16[2]), .S1(out_16[1]), .S0(out_16[0]), .Set(alu_4bit_5_set),
    .c4(out_20), .Pg(out_24), .Gg(out_28));
  ALU_4BIT alu_4bit_6 (
    .A3(A[7]), .A2(A[6]), .A1(A[5]), .A0(A[4]), .B3(B[7]), .B2(B[6]), .B1(B[5]), .B0(B[4]), .AInv(AInvert),
    .BInv(Bnegate), .C0(cla_2_c1), .Less(1'b0), .OPR(OPR), .OV_FLAG(out_38), .Set_Flag(out_42),
    .S3(out_46[3]), .S2(out_46[2]), .S1(out_46[1]), .S0(out_46[0]), .Set(alu_4bit_6_set), .c4(out_50),
    .Pg(out_54), .Gg(out_58));
  ALU_4BIT alu_4bit_7 (
    .A3(A[19]), .A2(A[18]), .A1(A[17]), .A0(A[16]), .B3(B[19]), .B2(B[18]), .B1(B[17]), .B0(B[16]),
    .AInv(AInvert), .BInv(Bnegate), .C0(cla_2_cout), .Less(undriven), .OPR(OPR), .OV_FLAG(out_9),
    .Set_Flag(out_13), .S3(out_17[3]), .S2(out_17[2]), .S1(out_17[1]), .S0(out_17[0]), .Set(alu_4bit_7_set),
    .c4(out_21), .Pg(out_25), .Gg(out_29));
  ALU_4BIT alu_4bit_8 (
    .A3(A[3]), .A2(A[2]), .A1(A[1]), .A0(A[0]), .B3(B[3]), .B2(B[2]), .B1(B[1]), .B0(B[0]), .AInv(AInvert),
    .BInv(Bnegate), .C0(Bnegate), .Less(alu_4bit_1_set), .OPR(OPR), .OV_FLAG(out_39), .Set_Flag(out_43),
    .S3(out_47[3]), .S2(out_47[2]), .S1(out_47[1]), .S0(out_47[0]), .c4(out_51), .Pg(out_55), .Gg(out_59));  // open: Set

  assign Result[27:0] = {out_15, out_16, out_17, out_44, out_45, out_46, out_47};
  assign S = Result[31:28];
endmodule

module PFA (
  input  X,
  input  Y,
  input  Cin,
  output Sum,
  output Pi,
  output Cout,
  output Gi
);

  wire and_1_out;

  xor xor_1 (Pi, X, Y);
  and and_1 (and_1_out, Pi, Cin);
  and and_2 (Gi, X, Y);
  xor xor_2 (Sum, Pi, Cin);
  or or_1 (Cout, and_1_out, Gi);
endmodule

module OV_Logic (
  input  A,
  input  B,
  input  Sub,
  input  R,
  output OV
);

  wire and_1_out, and_2_out, not_1_out, not_2_out, not_3_out, xor_1_out, xor_2_out;

  not not_1 (not_1_out, A);
  not not_2 (not_2_out, B);
  xor xor_1 (xor_1_out, not_2_out, Sub);
  xor xor_2 (xor_2_out, B, Sub);
  not not_3 (not_3_out, R);
  and and_1 (and_1_out, not_1_out, xor_1_out, R);
  and and_2 (and_2_out, A, xor_2_out, not_3_out);
  or or_1 (OV, and_1_out, 1'b0, and_2_out);
endmodule

module CLA (
  input  G0,
  input  C0,
  input  G1,
  input  G2,
  input  G3,
  input  P0,
  input  P1,
  input  P2,
  input  P3,
  output C3,
  output C1,
  output Cout,
  output C2,
  output Pg,
  output Gg
);

  wire and_1_out, and_2_out, and_3_out, and_4_out, and_5_out, and_6_out, and_8_out;

  or or_1 (Cout, G3, and_1_out);
  and and_1 (and_1_out, C3, P3);
  or or_2 (C3, G2, and_2_out);
  and and_2 (and_2_out, C2, P2);
  or or_3 (Gg, G3, and_3_out, and_4_out, and_5_out);
  and and_3 (and_3_out, P3, G2);
  and and_4 (and_4_out, P2, P3, G1);
  and and_5 (and_5_out, P3, P2, P1, G0);
  or or_4 (C2, G1, and_6_out);
  and and_6 (and_6_out, C1, P1);
  and and_7 (Pg, P0, P1, P2, P3);
  or or_5 (C1, G0, and_8_out);
  and and_8 (and_8_out, C0, P0);
endmodule

module ALU_4BIT (
  input  A3,
  input  A2,
  input  A1,
  input  A0,
  input  B3,
  input  B2,
  input  B1,
  input  B0,
  input  AInv,
  input  BInv,
  input  C0,
  input  Less,
  input  [1:0] OPR,
  output OV_FLAG,
  output Set_Flag,
  output S3,
  output S2,
  output S1,
  output S0,
  output Set,
  output c4,
  output Pg,
  output Gg
);

  wire and_1_out, and_2_out, and_3_out, and_4_out, cla_1_c1, cla_1_c2, cla_1_c3, multiplexer_1_out,
       multiplexer_2_out, multiplexer_4_out, multiplexer_5_out, multiplexer_7_out, multiplexer_8_out,
       multiplexer_10_out, multiplexer_11_out, not_1_out, not_2_out, not_3_out, not_4_out, not_5_out,
       not_6_out, not_7_out, not_8_out, or_1_out, or_2_out, or_3_out, or_4_out, ov_logic_2_ov, ov_logic_3_ov,
       ov_logic_4_ov, pfa_1_gi, pfa_1_pi, pfa_1_sum, pfa_2_cout, pfa_2_gi, pfa_2_pi, pfa_2_sum, pfa_3_cout,
       pfa_3_gi, pfa_3_pi, pfa_3_sum, pfa_4_cout, pfa_4_gi, pfa_4_pi, pfa_4_sum;

  not not_1 (not_1_out, A3);
  Multiplexer multiplexer_1 (.in0(A3), .in1(not_1_out), .out(multiplexer_1_out), .sel(AInv));
  not not_2 (not_2_out, B3);
  Multiplexer multiplexer_2 (.in0(B3), .in1(not_2_out), .out(multiplexer_2_out), .sel(BInv));
  OV_Logic ov_logic_1 (.A(multiplexer_1_out), .B(multiplexer_2_out), .Sub(BInv), .R(pfa_1_sum), .OV(OV_FLAG));
  and and_1 (and_1_out, multiplexer_1_out, multiplexer_2_out);
  or or_1 (or_1_out, multiplexer_1_out, multiplexer_2_out);
  PFA pfa_1 (
    .X(multiplexer_1_out), .Y(multiplexer_2_out), .Cin(cla_1_c3), .Sum(pfa_1_sum), .Pi(pfa_1_pi), .Cout(Set),
    .Gi(pfa_1_gi));
  Multiplexer #(.select(2)) multiplexer_3 (
    .in0(and_1_out), .in1(or_1_out), .in2(pfa_1_sum), .in3(1'b0), .out(S3), .sel(OPR));
  not not_3 (not_3_out, A2);
  Multiplexer multiplexer_4 (.in0(A2), .in1(not_3_out), .out(multiplexer_4_out), .sel(AInv));
  not not_4 (not_4_out, B2);
  Multiplexer multiplexer_5 (.in0(B2), .in1(not_4_out), .out(multiplexer_5_out), .sel(BInv));
  OV_Logic ov_logic_2 (.A(multiplexer_4_out), .B(multiplexer_5_out), .Sub(BInv), .R(pfa_2_sum), .OV(ov_logic_2_ov));
  and and_2 (and_2_out, multiplexer_4_out, multiplexer_5_out);
  or or_2 (or_2_out, multiplexer_4_out, multiplexer_5_out);
  PFA pfa_2 (
    .X(multiplexer_4_out), .Y(multiplexer_5_out), .Cin(cla_1_c2), .Sum(pfa_2_sum), .Pi(pfa_2_pi),
    .Cout(pfa_2_cout), .Gi(pfa_2_gi));
  Multiplexer #(.select(2)) multiplexer_6 (
    .in0(and_2_out), .in1(or_2_out), .in2(pfa_2_sum), .in3(1'b0), .out(S2), .sel(OPR));
  CLA cla_1 (
    .G0(pfa_4_gi), .C0(C0), .G1(pfa_3_gi), .G2(pfa_2_gi), .G3(pfa_1_gi), .P0(pfa_4_pi), .P1(pfa_3_pi),
    .P2(pfa_2_pi), .P3(pfa_1_pi), .C3(cla_1_c3), .C1(cla_1_c1), .Cout(c4), .C2(cla_1_c2), .Pg(Pg), .Gg(Gg));
  not not_5 (not_5_out, A1);
  not not_6 (not_6_out, B1);
  Multiplexer multiplexer_7 (.in0(A1), .in1(not_5_out), .out(multiplexer_7_out), .sel(AInv));
  Multiplexer multiplexer_8 (.in0(B1), .in1(not_6_out), .out(multiplexer_8_out), .sel(BInv));
  and and_3 (and_3_out, multiplexer_7_out, multiplexer_8_out);
  or or_3 (or_3_out, multiplexer_7_out, multiplexer_8_out);
  PFA pfa_3 (
    .X(multiplexer_7_out), .Y(multiplexer_8_out), .Cin(cla_1_c1), .Sum(pfa_3_sum), .Pi(pfa_3_pi),
    .Cout(pfa_3_cout), .Gi(pfa_3_gi));
  OV_Logic ov_logic_3 (.A(multiplexer_7_out), .B(multiplexer_8_out), .Sub(BInv), .R(pfa_3_sum), .OV(ov_logic_3_ov));
  Multiplexer #(.select(2)) multiplexer_9 (
    .in0(and_3_out), .in1(or_3_out), .in2(pfa_3_sum), .in3(1'b0), .out(S1), .sel(OPR));
  not not_7 (not_7_out, A0);
  not not_8 (not_8_out, B0);
  Multiplexer multiplexer_10 (.in0(A0), .in1(not_7_out), .out(multiplexer_10_out), .sel(AInv));
  Multiplexer multiplexer_11 (.in0(B0), .in1(not_8_out), .out(multiplexer_11_out), .sel(BInv));
  OV_Logic ov_logic_4 (.A(multiplexer_10_out), .B(multiplexer_11_out), .Sub(BInv), .R(pfa_4_sum), .OV(ov_logic_4_ov));
  and and_4 (and_4_out, multiplexer_10_out, multiplexer_11_out);
  or or_4 (or_4_out, multiplexer_10_out, multiplexer_11_out);
  PFA pfa_4 (
    .X(multiplexer_10_out), .Y(multiplexer_11_out), .Cin(C0), .Sum(pfa_4_sum), .Pi(pfa_4_pi),
    .Cout(pfa_4_cout), .Gi(pfa_4_gi));
  Multiplexer #(.select(2)) multiplexer_12 (
    .in0(and_4_out), .in1(or_4_out), .in2(pfa_4_sum), .in3(Less), .out(S0), .sel(OPR));

  assign Set_Flag = Set;
endmodule

module CLA_2 (
  input  G0,
  input  G1,
  input  C0,
  input  P1,
  input  P0,
  output C1,
  output Cout
);

  wire and_1_out, and_2_out;

  or or_1 (Cout, G1, and_1_out);
  and and_1 (and_1_out, C1, P1);
  or or_2 (C1, G0, and_2_out);
  and and_2 (and_2_out, C0, P0);
endmodule
