// Logisim project ALU_CONTROL.circ as structural Verilog: 1 circuit, main circuit main
module main (
  input  [1:0] ALUOp,
  input  [5:0] F,
  output [3:0] Output_to_ALU
);

  wire and_1_out, not_1_out, not_2_out, not_3_out, or_1_out;

  or or_1 (or_1_out, F[3], F[0]);
  not not_1 (not_1_out, ALUOp[0]);
  and and_1 (and_1_out, ALUOp[1], F[1]);
  not not_2 (not_2_out, ALUOp[1]);
  not not_3 (not_3_out, F[2]);
  and and_2 (Output_to_ALU[0], ALUOp[1], or_1_out);
  and and_3 (Output_to_ALU[3], ALUOp[0], not_1_out);
  or or_2 (Output_to_ALU[2], ALUOp[0], and_1_out);
  or or_3 (Output_to_ALU[1], not_2_out, not_3_out);
endmodule
