// Logisim project ALU_CONTROL_ROM.circ as structural Verilog: 1 circuit, main circuit main
module main (
  input  [7:0] in_1,
  output [3:0] out_2
);

  ROM #(.dataWidth(4)) rom_1 (.addr(in_1), .data(out_2));

  // Notes on the sheet:
  //   contents of rom_1 (hex, n*v repeats v):
  //   64*2 64*6 2 0 6 0 0 1 4*0 7 5*0 2 0 6 0 0 1 4*0 7 5*0 2 0 6 0 0 1 4*0 7 5*0 2 0 6 0 0 1 4*0 7
endmodule
