// Logisim project DataMemory.circ as structural Verilog: 1 circuit, main circuit main
module main (
  input  [23:0] in_1,
  input  in_2,
  input  in_3,
  input  [31:0] in_4,
  output [31:0] out_5
);

  wire clock_1_out;

  Clock clock_1 (.out(clock_1_out));
  RAM #(.addrWidth(24), .dataWidth(32)) ram_1 (
    .addr(in_1), .we(in_2), .oe(in_3), .clk(clock_1_out), .din(in_4), .dout(out_5));
endmodule
