// Logisim project File_register_medium.circ as structural Verilog: 1 circuit, main circuit main
module main (
  input  [7:0] WriteData,
  input  CLK,
  input  [2:0] Read_Reg_1,
  input  [2:0] Read_Reg_2,
  input  RegWrite,
  input  [2:0] WriteReg,
  output [7:0] Output_1,
  output [7:0] Output_2
);

  wire and_1_out, and_2_out, and_3_out, and_4_out, and_5_out, and_6_out, and_7_out, decoder_1_out1,
       decoder_1_out2, decoder_1_out3, decoder_1_out4, decoder_1_out5, decoder_1_out6, decoder_1_out7;
  wire [7:0] d_ff_50_q, d_ff_51_q, d_ff_52_q, d_ff_53_q, d_ff_54_q, d_ff_55_q, d_ff_56_q;

  Decoder #(.select(3)) decoder_1 (
    .out1(decoder_1_out1), .out2(decoder_1_out2), .out3(decoder_1_out3), .out4(decoder_1_out4),
    .out5(decoder_1_out5), .out6(decoder_1_out6), .out7(decoder_1_out7), .sel(WriteReg), .en(RegWrite));  // open: out0
  and and_1 (and_1_out, CLK, decoder_1_out1);
  and and_2 (and_2_out, CLK, decoder_1_out2);
  and and_3 (and_3_out, CLK, decoder_1_out3);
  and and_4 (and_4_out, CLK, decoder_1_out4);
  and and_5 (and_5_out, CLK, decoder_1_out5);
  and and_6 (and_6_out, CLK, decoder_1_out6);
  and and_7 (and_7_out, CLK, decoder_1_out7);
  D_Flip_Flop d_ff_1 (.D(WriteData[7]), .clk(and_1_out), .Q(d_ff_50_q[7]), .preset(1'b0), .reset(1'b0));  // open: Qn
  D_Flip_Flop d_ff_2 (.D(WriteData[7]), .clk(and_2_out), .Q(d_ff_51_q[7]), .preset(1'b0), .reset(1'b0));  // open: Qn
  D_Flip_Flop d_ff_3 (.D(WriteData[7]), .clk(and_3_out), .Q(d_ff_52_q[7]), .preset(1'b0), .reset(1'b0));  // open: Qn
  D_Flip_Flop d_ff_4 (.D(WriteData[7]), .clk(and_4_out), .Q(d_ff_53_q[7]), .preset(1'b0), .reset(1'b0));  // open: Qn
  D_Flip_Flop d_ff_5 (.D(WriteData[7]), .clk(and_5_out), .Q(d_ff_54_q[7]), .preset(1'b0), .reset(1'b0));  // open: Qn
  D_Flip_Flop d_ff_6 (.D(WriteData[7]), .clk(and_6_out), .Q(d_ff_55_q[7]), .preset(1'b0), .reset(1'b0));  // open: Qn
  D_Flip_Flop d_ff_7 (.D(WriteData[7]), .clk(and_7_out), .Q(d_ff_56_q[7]), .preset(1'b0), .reset(1'b0));  // open: Qn
  D_Flip_Flop d_ff_8 (.D(WriteData[6]), .clk(and_1_out), .Q(d_ff_50_q[6]), .preset(1'b0), .reset(1'b0));  // open: Qn
  D_Flip_Flop d_ff_9 (.D(WriteData[6]), .clk(and_2_out), .Q(d_ff_51_q[6]), .preset(1'b0), .reset(1'b0));  // open: Qn
  D_Flip_Flop d_ff_10 (.D(WriteData[6]), .clk(and_3_out), .Q(d_ff_52_q[6]), .preset(1'b0), .reset(1'b0));  // open: Qn
  D_Flip_Flop d_ff_11 (.D(WriteData[6]), .clk(and_4_out), .Q(d_ff_53_q[6]), .preset(1'b0), .reset(1'b0));  // open: Qn
  D_Flip_Flop d_ff_12 (.D(WriteData[6]), .clk(and_5_out), .Q(d_ff_54_q[6]), .preset(1'b0), .reset(1'b0));  // open: Qn
  D_Flip_Flop d_ff_13 (.D(WriteData[6]), .clk(and_6_out), .Q(d_ff_55_q[6]), .preset(1'b0), .reset(1'b0));  // open: Qn
  D_Flip_Flop d_ff_14 (.D(WriteData[6]), .clk(and_7_out), .Q(d_ff_56_q[6]), .preset(1'b0), .reset(1'b0));  // open: Qn
  D_Flip_Flop d_ff_15 (.D(WriteData[5]), .clk(and_1_out), .Q(d_ff_50_q[5]), .preset(1'b0), .reset(1'b0));  // open: Qn
  D_Flip_Flop d_ff_16 (.D(WriteData[5]), .clk(and_2_out), .Q(d_ff_51_q[5]), .preset(1'b0), .reset(1'b0));  // open: Qn
  D_Flip_Flop d_ff_17 (.D(WriteData[5]), .clk(and_3_out), .Q(d_ff_52_q[5]), .preset(1'b0), .reset(1'b0));  // open: Qn
  D_Flip_Flop d_ff_18 (.D(WriteData[5]), .clk(and_4_out), .Q(d_ff_53_q[5]), .preset(1'b0), .reset(1'b0));  // open: Qn
  D_Flip_Flop d_ff_19 (.D(WriteData[5]), .clk(and_5_out), .Q(d_ff_54_q[5]), .preset(1'b0), .reset(1'b0));  // open: Qn
  D_Flip_Flop d_ff_20 (.D(WriteData[5]), .clk(and_6_out), .Q(d_ff_55_q[5]), .preset(1'b0), .reset(1'b0));  // open: Qn
  D_Flip_Flop d_ff_21 (.D(WriteData[5]), .clk(and_7_out), .Q(d_ff_56_q[5]), .preset(1'b0), .reset(1'b0));  // open: Qn
  D_Flip_Flop d_ff_22 (.D(WriteData[4]), .clk(and_1_out), .Q(d_ff_50_q[4]), .preset(1'b0), .reset(1'b0));  // open: Qn
  D_Flip_Flop d_ff_23 (.D(WriteData[4]), .clk(and_2_out), .Q(d_ff_51_q[4]), .preset(1'b0), .reset(1'b0));  // open: Qn
  D_Flip_Flop d_ff_24 (.D(WriteData[4]), .clk(and_3_out), .Q(d_ff_52_q[4]), .preset(1'b0), .reset(1'b0));  // open: Qn
  D_Flip_Flop d_ff_25 (.D(WriteData[4]), .clk(and_4_out), .Q(d_ff_53_q[4]), .preset(1'b0), .reset(1'b0));  // open: Qn
  D_Flip_Flop d_ff_26 (.D(WriteData[4]), .clk(and_5_out), .Q(d_ff_54_q[4]), .preset(1'b0), .reset(1'b0));  // open: Qn
  D_Flip_Flop d_ff_27 (.D(WriteData[4]), .clk(and_6_out), .Q(d_ff_55_q[4]), .preset(1'b0), .reset(1'b0));  // open: Qn
  D_Flip_Flop d_ff_28 (.D(WriteData[4]), .clk(and_7_out), .Q(d_ff_56_q[4]), .preset(1'b0), .reset(1'b0));  // open: Qn
  D_Flip_Flop d_ff_29 (.D(WriteData[3]), .clk(and_1_out), .Q(d_ff_50_q[3]), .preset(1'b0), .reset(1'b0));  // open: Qn
  D_Flip_Flop d_ff_30 (.D(WriteData[3]), .clk(and_2_out), .Q(d_ff_51_q[3]), .preset(1'b0), .reset(1'b0));  // open: Qn
  D_Flip_Flop d_ff_31 (.D(WriteData[3]), .clk(and_3_out), .Q(d_ff_52_q[3]), .preset(1'b0), .reset(1'b0));  // open: Qn
  D_Flip_Flop d_ff_32 (.D(WriteData[3]), .clk(and_4_out), .Q(d_ff_53_q[3]), .preset(1'b0), .reset(1'b0));  // open: Qn
  D_Flip_Flop d_ff_33 (.D(WriteData[3]), .clk(and_5_out), .Q(d_ff_54_q[3]), .preset(1'b0), .reset(1'b0));  // open: Qn
  D_Flip_Flop d_ff_34 (.D(WriteData[3]), .clk(and_6_out), .Q(d_ff_55_q[3]), .preset(1'b0), .reset(1'b0));  // open: Qn
  D_Flip_Flop d_ff_35 (.D(WriteData[3]), .clk(and_7_out), .Q(d_ff_56_q[3]), .preset(1'b0), .reset(1'b0));  // open: Qn
  D_Flip_Flop d_ff_36 (.D(WriteData[2]), .clk(and_1_out), .Q(d_ff_50_q[2]), .preset(1'b0), .reset(1'b0));  // open: Qn
  D_Flip_Flop d_ff_37 (.D(WriteData[2]), .clk(and_2_out), .Q(d_ff_51_q[2]), .preset(1'b0), .reset(1'b0));  // open: Qn
  D_Flip_Flop d_ff_38 (.D(WriteData[2]), .clk(and_3_out), .Q(d_ff_52_q[2]), .preset(1'b0), .reset(1'b0));  // open: Qn
  D_Flip_Flop d_ff_39 (.D(WriteData[2]), .clk(and_4_out), .Q(d_ff_53_q[2]), .preset(1'b0), .reset(1'b0));  // open: Qn
  D_Flip_Flop d_ff_40 (.D(WriteData[2]), .clk(and_5_out), .Q(d_ff_54_q[2]), .preset(1'b0), .reset(1'b0));  // open: Qn
  D_Flip_Flop d_ff_41 (.D(WriteData[2]), .clk(and_6_out), .Q(d_ff_55_q[2]), .preset(1'b0), .reset(1'b0));  // open: Qn
  D_Flip_Flop d_ff_42 (.D(WriteData[2]), .clk(and_7_out), .Q(d_ff_56_q[2]), .preset(1'b0), .reset(1'b0));  // open: Qn
  D_Flip_Flop d_ff_43 (.D(WriteData[1]), .clk(and_1_out), .Q(d_ff_50_q[1]), .preset(1'b0), .reset(1'b0));  // open: Qn
  D_Flip_Flop d_ff_44 (.D(WriteData[1]), .clk(and_2_out), .Q(d_ff_51_q[1]), .preset(1'b0), .reset(1'b0));  // open: Qn
  D_Flip_Flop d_ff_45 (.D(WriteData[1]), .clk(and_3_out), .Q(d_ff_52_q[1]), .preset(1'b0), .reset(1'b0));  // open: Qn
  D_Flip_Flop d_ff_46 (.D(WriteData[1]), .clk(and_4_out), .Q(d_ff_53_q[1]), .preset(1'b0), .reset(1'b0));  // open: Qn
  D_Flip_Flop d_ff_47 (.D(WriteData[1]), .clk(and_5_out), .Q(d_ff_54_q[1]), .preset(1'b0), .reset(1'b0));  // open: Qn
  D_Flip_Flop d_ff_48 (.D(WriteData[1]), .clk(and_6_out), .Q(d_ff_55_q[1]), .reset(1'b0));  // open: Qn, preset
  D_Flip_Flop d_ff_49 (.D(WriteData[1]), .clk(and_7_out), .Q(d_ff_56_q[1]), .preset(1'b0), .reset(1'b0));  // open: Qn
  D_Flip_Flop d_ff_50 (.D(WriteData[0]), .clk(and_1_out), .Q(d_ff_50_q[0]), .preset(1'b0), .reset(1'b0));  // open: Qn
  D_Flip_Flop d_ff_51 (.D(WriteData[0]), .clk(and_2_out), .Q(d_ff_51_q[0]), .preset(1'b0), .reset(1'b0));  // open: Qn
  D_Flip_Flop d_ff_52 (.D(WriteData[0]), .clk(and_3_out), .Q(d_ff_52_q[0]), .preset(1'b0), .reset(1'b0));  // open: Qn
  D_Flip_Flop d_ff_53 (.D(WriteData[0]), .clk(and_4_out), .Q(d_ff_53_q[0]), .preset(1'b0), .reset(1'b0));  // open: Qn
  D_Flip_Flop d_ff_54 (.D(WriteData[0]), .clk(and_5_out), .Q(d_ff_54_q[0]), .preset(1'b0), .reset(1'b0));  // open: Qn
  D_Flip_Flop d_ff_55 (.D(WriteData[0]), .clk(and_6_out), .Q(d_ff_55_q[0]), .preset(1'b0), .reset(1'b0));  // open: Qn
  D_Flip_Flop d_ff_56 (.D(WriteData[0]), .clk(and_7_out), .Q(d_ff_56_q[0]), .preset(1'b0), .reset(1'b0));  // open: Qn
  Multiplexer #(.select(3), .width(8)) multiplexer_1 (
    .in0({8{1'b0}}), .in1(d_ff_50_q), .in2(d_ff_51_q), .in3(d_ff_52_q), .in4(d_ff_53_q), .in5(d_ff_54_q),
    .in6(d_ff_55_q), .in7(d_ff_56_q), .out(Output_1), .sel(Read_Reg_1));
  Multiplexer #(.select(3), .width(8)) multiplexer_2 (
    .in0({8{1'b0}}), .in1(d_ff_50_q), .in2(d_ff_51_q), .in3(d_ff_52_q), .in4(d_ff_53_q), .in5(d_ff_54_q),
    .in6(d_ff_55_q), .in7(d_ff_56_q), .out(Output_2), .sel(Read_Reg_2));
endmodule
