// Logisim project File_register_simple.circ as structural Verilog: 1 circuit, main circuit main
module main (
  input  [3:0] WriteData,
  input  RegWrite,
  input  [1:0] ReadReg_1,
  input  [1:0] WriteReg,
  input  [1:0] ReadReg_2,
  output [3:0] Output_1,
  output [3:0] Output_2
);

  wire and_1_out, and_2_out, and_3_out, and_4_out, CLK_out, decoder_1_out0, decoder_1_out1, decoder_1_out2,
       decoder_1_out3;
  wire [3:0] d_ff_13_q, d_ff_14_q, d_ff_15_q, d_ff_16_q;

  Clock CLK (.out(CLK_out));
  Decoder #(.select(2)) decoder_1 (
    .out0(decoder_1_out0), .out1(decoder_1_out1), .out2(decoder_1_out2), .out3(decoder_1_out3),
    .sel(WriteReg), .en(RegWrite));
  and and_1 (and_1_out, CLK_out, decoder_1_out1);
  and and_2 (and_2_out, CLK_out, decoder_1_out2);
  and and_3 (and_3_out, CLK_out, decoder_1_out3);
  and and_4 (and_4_out, CLK_out, decoder_1_out0);
  D_Flip_Flop d_ff_1 (.D(WriteData[3]), .clk(and_4_out), .Q(d_ff_13_q[3]), .preset(1'b0), .reset(1'b0));  // open: Qn
  D_Flip_Flop d_ff_2 (.D(WriteData[3]), .clk(and_1_out), .Q(d_ff_14_q[3]), .preset(1'b0), .reset(1'b0));  // open: Qn
  D_Flip_Flop d_ff_3 (.D(WriteData[3]), .clk(and_2_out), .Q(d_ff_15_q[3]), .preset(1'b0), .reset(1'b0));  // open: Qn
  D_Flip_Flop d_ff_4 (.D(WriteData[3]), .clk(and_3_out), .Q(d_ff_16_q[3]), .preset(1'b0), .reset(1'b0));  // open: Qn
  D_Flip_Flop d_ff_5 (.D(WriteData[2]), .clk(and_4_out), .Q(d_ff_13_q[2]), .preset(1'b0), .reset(1'b0));  // open: Qn
  D_Flip_Flop d_ff_6 (.D(WriteData[2]), .clk(and_1_out), .Q(d_ff_14_q[2]), .preset(1'b0), .reset(1'b0));  // open: Qn
  D_Flip_Flop d_ff_7 (.D(WriteData[2]), .clk(and_2_out), .Q(d_ff_15_q[2]), .preset(1'b0), .reset(1'b0));  // open: Qn
  D_Flip_Flop d_ff_8 (.D(WriteData[2]), .clk(and_3_out), .Q(d_ff_16_q[2]), .preset(1'b0), .reset(1'b0));  // open: Qn
  D_Flip_Flop d_ff_9 (.D(WriteData[1]), .clk(and_4_out), .Q(d_ff_13_q[1]), .preset(1'b0), .reset(1'b0));  // open: Qn
  D_Flip_Flop d_ff_10 (.D(WriteData[1]), .clk(and_1_out), .Q(d_ff_14_q[1]), .preset(1'b0), .reset(1'b0));  // open: Qn
  D_Flip_Flop d_ff_11 (.D(WriteData[1]), .clk(and_2_out), .Q(d_ff_15_q[1]), .preset(1'b0), .reset(1'b0));  // open: Qn
  D_Flip_Flop d_ff_12 (.D(WriteData[1]), .clk(and_3_out), .Q(d_ff_16_q[1]), .preset(1'b0), .reset(1'b0));  // open: Qn
  D_Flip_Flop d_ff_13 (.D(WriteData[0]), .clk(and_4_out), .Q(d_ff_13_q[0]), .preset(1'b0), .reset(1'b0));  // open: Qn
  D_Flip_Flop d_ff_14 (.D(WriteData[0]), .clk(and_1_out), .Q(d_ff_14_q[0]), .preset(1'b0), .reset(1'b0));  // open: Qn
  D_Flip_Flop d_ff_15 (.D(WriteData[0]), .clk(and_2_out), .Q(d_ff_15_q[0]), .preset(1'b0), .reset(1'b0));  // open: Qn
  D_Flip_Flop d_ff_16 (.D(WriteData[0]), .clk(and_3_out), .Q(d_ff_16_q[0]), .preset(1'b0), .reset(1'b0));  // open: Qn
  Multiplexer #(.select(2), .width(4)) multiplexer_1 (
    .in0(d_ff_13_q), .in1(d_ff_14_q), .in2(d_ff_15_q), .in3(d_ff_16_q), .out(Output_1), .sel(ReadReg_1));
  Multiplexer #(.select(2), .width(4)) multiplexer_2 (
    .in0(d_ff_13_q), .in1(d_ff_14_q), .in2(d_ff_15_q), .in3(d_ff_16_q), .out(Output_2), .sel(ReadReg_2));
endmodule
