// Logisim project InstructionMemory.circ as structural Verilog: 1 circuit, main circuit main
module main (
  input  in_1,
  input  [31:0] in_2,
  output [31:0] out_3
);

  wire button_1_out, clock_1_out, multiplexer_1_out;
  wire [7:0] multiplexer_2_out, multiplexer_3_out, multiplexer_4_out, multiplexer_5_out, multiplexer_6_out,
       multiplexer_7_out, multiplexer_8_out, multiplexer_9_out, multiplexer_10_out, multiplexer_11_out,
       multiplexer_12_out, multiplexer_13_out, multiplexer_14_out, multiplexer_15_out, multiplexer_16_out,
       multiplexer_17_out, multiplexer_18_out, multiplexer_19_out, multiplexer_20_out, multiplexer_21_out,
       multiplexer_22_out, multiplexer_23_out, multiplexer_24_out, multiplexer_25_out, rom_1_p2, rom_1_p3,
       rom_1_p4, rom_1_p5, rom_2_p2, rom_2_p3, rom_2_p4, rom_2_p5, rom_3_p2, rom_3_p3, rom_3_p4, rom_3_p5,
       rom_4_p2, rom_4_p3, rom_4_p4, rom_4_p5, rom_5_p2, rom_5_p3, rom_5_p4, rom_5_p5, rom_6_p2, rom_6_p3,
       rom_6_p4, rom_6_p5, rom_7_p2, rom_7_p3, rom_7_p4, rom_7_p5, rom_8_p2, rom_8_p3, rom_8_p4, rom_8_p5;
  wire [31:0] adder_1_out, counter_1_q;

  Adder #(.width(32)) adder_1 (.a(counter_1_q), .b(in_2), .out(adder_1_out));  // open: cin, cout
  Counter #(.max('hffffffff), .width(32)) counter_1 (
    .load(clock_1_out), .D(adder_1_out), .Q(counter_1_q), .up(in_1), .clk(clock_1_out),
    .clr(multiplexer_1_out));  // open: count, carry
  Clock clock_1 (.out(clock_1_out));
  Button button_1 (.out(button_1_out));
  Multiplexer multiplexer_1 (.in0(counter_1_q[27]), .in1(1'b1), .out(multiplexer_1_out), .sel(button_1_out));
  // ROM #(.addrWidth(24), .line("quad")) rom_1: pin names not known; wires that end beside it: counter_1_q[23:0], rom_1_p2, rom_1_p3, rom_1_p4, rom_1_p5
  // ROM #(.addrWidth(24), .line("quad")) rom_2: pin names not known; wires that end beside it: counter_1_q[23:0], rom_2_p2, rom_2_p3, rom_2_p4, rom_2_p5
  // ROM #(.addrWidth(24), .line("quad")) rom_3: pin names not known; wires that end beside it: counter_1_q[23:0], rom_3_p2, rom_3_p3, rom_3_p4, rom_3_p5
  // ROM #(.addrWidth(24), .line("quad")) rom_4: pin names not known; wires that end beside it: counter_1_q[23:0], rom_4_p2, rom_4_p3, rom_4_p4, rom_4_p5
  // ROM #(.addrWidth(24), .line("quad")) rom_5: pin names not known; wires that end beside it: counter_1_q[23:0], rom_5_p2, rom_5_p3, rom_5_p4, rom_5_p5
  // ROM #(.addrWidth(24), .line("quad")) rom_6: pin names not known; wires that end beside it: counter_1_q[23:0], rom_6_p2, rom_6_p3, rom_6_p4, rom_6_p5
  // ROM #(.addrWidth(24), .line("quad")) rom_7: pin names not known; wires that end beside it: counter_1_q[23:0], rom_7_p2, rom_7_p3, rom_7_p4, rom_7_p5
  // ROM #(.addrWidth(24), .line("quad")) rom_8: pin names not known; wires that end beside it: counter_1_q[23:0], rom_8_p2, rom_8_p3, rom_8_p4, rom_8_p5
  Multiplexer #(.width(8)) multiplexer_2 (
    .in0(rom_1_p2), .in1(rom_2_p2), .out(multiplexer_2_out), .sel(counter_1_q[24]));
  Multiplexer #(.width(8)) multiplexer_3 (
    .in0(rom_1_p3), .in1(rom_2_p3), .out(multiplexer_3_out), .sel(counter_1_q[24]));
  Multiplexer #(.width(8)) multiplexer_4 (
    .in0(rom_1_p4), .in1(rom_2_p4), .out(multiplexer_4_out), .sel(counter_1_q[24]));
  Multiplexer #(.width(8)) multiplexer_5 (
    .in0(rom_1_p5), .in1(rom_2_p5), .out(multiplexer_5_out), .sel(counter_1_q[24]));
  Multiplexer #(.width(8)) multiplexer_6 (
    .in0(rom_3_p2), .in1(rom_4_p2), .out(multiplexer_6_out), .sel(counter_1_q[24]));
  Multiplexer #(.width(8)) multiplexer_7 (
    .in0(rom_3_p3), .in1(rom_4_p3), .out(multiplexer_7_out), .sel(counter_1_q[24]));
  Multiplexer #(.width(8)) multiplexer_8 (
    .in0(rom_3_p4), .in1(rom_4_p4), .out(multiplexer_8_out), .sel(counter_1_q[24]));
  Multiplexer #(.width(8)) multiplexer_9 (
    .in0(rom_3_p5), .in1(rom_4_p5), .out(multiplexer_9_out), .sel(counter_1_q[24]));
  Multiplexer #(.width(8)) multiplexer_10 (
    .in0(rom_5_p2), .in1(rom_6_p2), .out(multiplexer_10_out), .sel(counter_1_q[24]));
  Multiplexer #(.width(8)) multiplexer_11 (
    .in0(rom_5_p3), .in1(rom_6_p3), .out(multiplexer_11_out), .sel(counter_1_q[24]));
  Multiplexer #(.width(8)) multiplexer_12 (
    .in0(rom_5_p4), .in1(rom_6_p4), .out(multiplexer_12_out), .sel(counter_1_q[24]));
  Multiplexer #(.width(8)) multiplexer_13 (
    .in0(rom_5_p5), .in1(rom_6_p5), .out(multiplexer_13_out), .sel(counter_1_q[24]));
  Multiplexer #(.width(8)) multiplexer_14 (
    .in0(rom_7_p2), .in1(rom_8_p2), .out(multiplexer_14_out), .sel(counter_1_q[24]));
  Multiplexer #(.width(8)) multiplexer_15 (
    .in0(rom_7_p3), .in1(rom_8_p3), .out(multiplexer_15_out), .sel(counter_1_q[24]));
  Multiplexer #(.width(8)) multiplexer_16 (
    .in0(rom_7_p4), .in1(rom_8_p4), .out(multiplexer_16_out), .sel(counter_1_q[24]));
  Multiplexer #(.width(8)) multiplexer_17 (
    .in0(rom_7_p5), .in1(rom_8_p5), .out(multiplexer_17_out), .sel(counter_1_q[24]));
  Multiplexer #(.width(8)) multiplexer_18 (
    .in0(multiplexer_2_out), .in1(multiplexer_6_out), .out(multiplexer_18_out), .sel(counter_1_q[25]));
  Multiplexer #(.width(8)) multiplexer_19 (
    .in0(multiplexer_3_out), .in1(multiplexer_7_out), .out(multiplexer_19_out), .sel(counter_1_q[25]));
  Multiplexer #(.width(8)) multiplexer_20 (
    .in0(multiplexer_4_out), .in1(multiplexer_8_out), .out(multiplexer_20_out), .sel(counter_1_q[25]));
  Multiplexer #(.width(8)) multiplexer_21 (
    .in0(multiplexer_5_out), .in1(multiplexer_9_out), .out(multiplexer_21_out), .sel(counter_1_q[25]));
  Multiplexer #(.width(8)) multiplexer_22 (
    .in0(multiplexer_10_out), .in1(multiplexer_14_out), .out(multiplexer_22_out), .sel(counter_1_q[25]));
  Multiplexer #(.width(8)) multiplexer_23 (
    .in0(multiplexer_11_out), .in1(multiplexer_15_out), .out(multiplexer_23_out), .sel(counter_1_q[25]));
  Multiplexer #(.width(8)) multiplexer_24 (
    .in0(multiplexer_12_out), .in1(multiplexer_16_out), .out(multiplexer_24_out), .sel(counter_1_q[25]));
  Multiplexer #(.width(8)) multiplexer_25 (
    .in0(multiplexer_13_out), .in1(multiplexer_17_out), .out(multiplexer_25_out), .sel(counter_1_q[25]));
  Multiplexer #(.width(32)) multiplexer_26 (
    .in0({multiplexer_18_out, multiplexer_19_out, multiplexer_20_out, multiplexer_21_out}),
    .in1({multiplexer_22_out, multiplexer_23_out, multiplexer_24_out, multiplexer_25_out}), .out(out_3),
    .sel(counter_1_q[26]));

  // Notes on the sheet:
  //   in_2: initial=0x4
  //   contents of rom_1 (hex, n*v repeats v):
  //   ab cd ef 56 12 13 14 41 ff 78 34 45 67
  //   contents of rom_2 (hex, n*v repeats v):
  //   33 44 55 66 1 88 bb ff ff 78 34 45 67
  //   contents of rom_3 (hex, n*v repeats v):
  //   44 ff 12 56 12 13 14 41 ff 78 34 45 67
  //   contents of rom_4 (hex, n*v repeats v):
  //   ff 44 55 66 aa 88 bb ff ff 78 34 45 67
  //   contents of rom_5 (hex, n*v repeats v):
  //   4*aa 12 13 14 41 ff 78 34 45 67
  //   contents of rom_6 (hex, n*v repeats v):
  //   33 44 55 66 1 88 bb ff ff 78 34 45 67
  //   contents of rom_7 (hex, n*v repeats v):
  //   44 ff 12 56 12 13 14 41 ff 78 34 45 67
  //   contents of rom_8 (hex, n*v repeats v):
  //   dd ee ff 66 aa 88 bb ff ff 78 34 45 67
endmodule
