// Logisim project ProgramCounter.circ as structural Verilog: 1 circuit, main circuit main
module main (
  input  in_1,
  input  in_2,
  output [31:0] out_3
);

  wire clock_1_out;
  wire [31:0] adder_1_out;

  Adder #(.width(32)) adder_1 (.a(out_3), .b(32'h4), .out(adder_1_out));  // open: cin, cout
  Clock clock_1 (.out(clock_1_out));
  Register #(.width(32)) register_1 (.D(adder_1_out), .en(in_1), .clk(clock_1_out), .Q(out_3), .clr(in_2));
endmodule
