// Logisim project RAM_SIMPLE_.circ as structural Verilog: 1 circuit, main circuit main
module main (
  input  [3:0] Data,
  input  WriteEN,
  input  Address,
  input  ReadEN,
  output [3:0] Out_put
);

  wire and_1_out, and_2_out, clock_1_out, decoder_1_out0, decoder_1_out1;
  wire [3:0] d_ff_7_q, d_ff_8_q, multiplexer_1_out, multiplexer_2_out;

  and and_1 (and_1_out, decoder_1_out0, WriteEN);
  and and_2 (and_2_out, decoder_1_out1, WriteEN);
  Multiplexer #(.width(4)) multiplexer_1 (
    .in0(multiplexer_1_out), .in1(Data), .out(multiplexer_1_out), .sel(and_1_out));
  Multiplexer #(.width(4)) multiplexer_2 (
    .in0(multiplexer_2_out), .in1(Data), .out(multiplexer_2_out), .sel(and_2_out));
  Clock clock_1 (.out(clock_1_out));
  Decoder #(.enable("false")) decoder_1 (.out0(decoder_1_out0), .out1(decoder_1_out1), .sel(Address));
  D_Flip_Flop d_ff_1 (.D(multiplexer_1_out[3]), .clk(clock_1_out), .Q(d_ff_7_q[3]));  // open: Qn, preset, reset
  D_Flip_Flop d_ff_2 (.D(multiplexer_2_out[3]), .clk(clock_1_out), .Q(d_ff_8_q[3]));  // open: Qn, preset, reset
  D_Flip_Flop d_ff_3 (.D(multiplexer_1_out[2]), .clk(clock_1_out), .Q(d_ff_7_q[2]));  // open: Qn, preset, reset
  D_Flip_Flop d_ff_4 (.D(multiplexer_2_out[2]), .clk(clock_1_out), .Q(d_ff_8_q[2]));  // open: Qn, preset, reset
  D_Flip_Flop d_ff_5 (.D(multiplexer_1_out[1]), .clk(clock_1_out), .Q(d_ff_7_q[1]));  // open: Qn, preset, reset
  D_Flip_Flop d_ff_6 (.D(multiplexer_2_out[1]), .clk(clock_1_out), .Q(d_ff_8_q[1]));  // open: Qn, preset, reset
  D_Flip_Flop d_ff_7 (.D(multiplexer_1_out[0]), .clk(clock_1_out), .Q(d_ff_7_q[0]));  // open: Qn, preset, reset
  D_Flip_Flop d_ff_8 (.D(multiplexer_2_out[0]), .clk(clock_1_out), .Q(d_ff_8_q[0]));  // open: Qn, preset, reset
  Multiplexer #(.enable("true"), .width(4)) multiplexer_3 (
    .in0(d_ff_7_q), .in1(d_ff_8_q), .out(Out_put), .sel(Address), .en(ReadEN));
endmodule
