// Logisim project Register_File.circ as structural Verilog: 2 circuits, main circuit main
module main (
  input  CLK,
  input  RegWrite,
  input  [4:0] WriteReg,
  input  [31:0] WriteData,
  input  [4:0] Read_Reg_1,
  input  [4:0] Read_Reg_2,
  output [31:0] Output_1,
  output [31:0] Output_2
);

  wire and_1_out, and_2_out, and_3_out, and_4_out, and_5_out, and_6_out, and_7_out, and_8_out, and_9_out,
       and_10_out, and_11_out, and_12_out, and_13_out, and_14_out, and_15_out, and_16_out, and_17_out,
       and_18_out, and_19_out, and_20_out, and_21_out, and_22_out, and_23_out, and_24_out, and_25_out,
       and_26_out, and_27_out, and_28_out, and_29_out, and_30_out, and_31_out, decoder_1_out1,
       decoder_1_out2, decoder_1_out3, decoder_1_out4, decoder_1_out5, decoder_1_out6, decoder_1_out7,
       decoder_1_out8, decoder_1_out9, decoder_1_out10, decoder_1_out11, decoder_1_out12, decoder_1_out13,
       decoder_1_out14, decoder_1_out15;
  wire [15:0] decoder_1_out16;
  wire [31:0] reg_32bit_1_reg_out, reg_32bit_2_reg_out, reg_32bit_3_reg_out, reg_32bit_4_reg_out,
       reg_32bit_5_reg_out, reg_32bit_6_reg_out, reg_32bit_7_reg_out, reg_32bit_8_reg_out,
       reg_32bit_9_reg_out, reg_32bit_10_reg_out, reg_32bit_11_reg_out, reg_32bit_12_reg_out,
       reg_32bit_13_reg_out, reg_32bit_14_reg_out, reg_32bit_15_reg_out, reg_32bit_16_reg_out,
       reg_32bit_17_reg_out, reg_32bit_18_reg_out, reg_32bit_19_reg_out, reg_32bit_20_reg_out,
       reg_32bit_21_reg_out, reg_32bit_22_reg_out, reg_32bit_23_reg_out, reg_32bit_24_reg_out,
       reg_32bit_25_reg_out, reg_32bit_26_reg_out, reg_32bit_27_reg_out, reg_32bit_28_reg_out,
       reg_32bit_29_reg_out, reg_32bit_30_reg_out, reg_32bit_31_reg_out;

  Decoder #(.select(5)) decoder_1 (
    .out1(decoder_1_out1), .out2(decoder_1_out2), .out3(decoder_1_out3), .out4(decoder_1_out4),
    .out5(decoder_1_out5), .out6(decoder_1_out6), .out7(decoder_1_out7), .out8(decoder_1_out8),
    .out9(decoder_1_out9), .out10(decoder_1_out10), .out11(decoder_1_out11), .out12(decoder_1_out12),
    .out13(decoder_1_out13), .out14(decoder_1_out14), .out15(decoder_1_out15), .out16(decoder_1_out16[0]),
    .out17(decoder_1_out16[1]), .out18(decoder_1_out16[2]), .out19(decoder_1_out16[3]),
    .out20(decoder_1_out16[4]), .out21(decoder_1_out16[5]), .out22(decoder_1_out16[6]),
    .out23(decoder_1_out16[7]), .out24(decoder_1_out16[8]), .out25(decoder_1_out16[9]),
    .out26(decoder_1_out16[10]), .out27(decoder_1_out16[11]), .out28(decoder_1_out16[12]),
    .out29(decoder_1_out16[13]), .out30(decoder_1_out16[14]), .out31(decoder_1_out16[15]), .sel(WriteReg),
    .en(RegWrite));  // open: out0
  and and_1 (and_1_out, CLK, decoder_1_out1);
  and and_2 (and_2_out, CLK, decoder_1_out2);
  and and_3 (and_3_out, CLK, decoder_1_out3);
  and and_4 (and_4_out, CLK, decoder_1_out4);
  and and_5 (and_5_out, CLK, decoder_1_out5);
  and and_6 (and_6_out, CLK, decoder_1_out6);
  and and_7 (and_7_out, CLK, decoder_1_out7);
  and and_8 (and_8_out, CLK, decoder_1_out8);
  and and_9 (and_9_out, CLK, decoder_1_out9);
  and and_10 (and_10_out, CLK, decoder_1_out10);
  and and_11 (and_11_out, CLK, decoder_1_out11);
  and and_12 (and_12_out, CLK, decoder_1_out12);
  and and_13 (and_13_out, CLK, decoder_1_out13);
  and and_14 (and_14_out, CLK, decoder_1_out14);
  and and_15 (and_15_out, CLK, decoder_1_out15);
  Reg_32Bit reg_32bit_1 (.CLK(and_1_out), .Reg_Input(WriteData), .Reg_Out(reg_32bit_1_reg_out));
  Reg_32Bit reg_32bit_2 (.CLK(and_2_out), .Reg_Input(WriteData), .Reg_Out(reg_32bit_2_reg_out));
  Reg_32Bit reg_32bit_3 (.CLK(and_3_out), .Reg_Input(WriteData), .Reg_Out(reg_32bit_3_reg_out));
  Reg_32Bit reg_32bit_4 (.CLK(and_4_out), .Reg_Input(WriteData), .Reg_Out(reg_32bit_4_reg_out));
  Reg_32Bit reg_32bit_5 (.CLK(and_5_out), .Reg_Input(WriteData), .Reg_Out(reg_32bit_5_reg_out));
  Reg_32Bit reg_32bit_6 (.CLK(and_6_out), .Reg_Input(WriteData), .Reg_Out(reg_32bit_6_reg_out));
  Reg_32Bit reg_32bit_7 (.CLK(and_7_out), .Reg_Input(WriteData), .Reg_Out(reg_32bit_7_reg_out));
  Reg_32Bit reg_32bit_8 (.CLK(and_8_out), .Reg_Input(WriteData), .Reg_Out(reg_32bit_8_reg_out));
  Reg_32Bit reg_32bit_9 (.CLK(and_9_out), .Reg_Input(WriteData), .Reg_Out(reg_32bit_9_reg_out));
  Reg_32Bit reg_32bit_10 (.CLK(and_10_out), .Reg_Input(WriteData), .Reg_Out(reg_32bit_10_reg_out));
  Reg_32Bit reg_32bit_11 (.CLK(and_11_out), .Reg_Input(WriteData), .Reg_Out(reg_32bit_11_reg_out));
  Reg_32Bit reg_32bit_12 (.CLK(and_12_out), .Reg_Input(WriteData), .Reg_Out(reg_32bit_12_reg_out));
  Reg_32Bit reg_32bit_13 (.CLK(and_13_out), .Reg_Input(WriteData), .Reg_Out(reg_32bit_13_reg_out));
  Reg_32Bit reg_32bit_14 (.CLK(and_14_out), .Reg_Input(WriteData), .Reg_Out(reg_32bit_14_reg_out));
  Reg_32Bit reg_32bit_15 (.CLK(and_15_out), .Reg_Input(WriteData), .Reg_Out(reg_32bit_15_reg_out));
  and and_16 (and_16_out, CLK, decoder_1_out16[0]);
  and and_17 (and_17_out, CLK, decoder_1_out16[1]);
  and and_18 (and_18_out, CLK, decoder_1_out16[2]);
  and and_19 (and_19_out, CLK, decoder_1_out16[3]);
  and and_20 (and_20_out, CLK, decoder_1_out16[4]);
  and and_21 (and_21_out, CLK, decoder_1_out16[5]);
  and and_22 (and_22_out, CLK, decoder_1_out16[6]);
  and and_23 (and_23_out, CLK, decoder_1_out16[7]);
  and and_24 (and_24_out, CLK, decoder_1_out16[8]);
  and and_25 (and_25_out, CLK, decoder_1_out16[9]);
  and and_26 (and_26_out, CLK, decoder_1_out16[10]);
  and and_27 (and_27_out, CLK, decoder_1_out16[11]);
  and and_28 (and_28_out, CLK, decoder_1_out16[12]);
  and and_29 (and_29_out, CLK, decoder_1_out16[13]);
  and and_30 (and_30_out, CLK, decoder_1_out16[14]);
  and and_31 (and_31_out, CLK, decoder_1_out16[15]);
  Reg_32Bit reg_32bit_16 (.CLK(and_16_out), .Reg_Input(WriteData), .Reg_Out(reg_32bit_16_reg_out));
  Reg_32Bit reg_32bit_17 (.CLK(and_17_out), .Reg_Input(WriteData), .Reg_Out(reg_32bit_17_reg_out));
  Reg_32Bit reg_32bit_18 (.CLK(and_18_out), .Reg_Input(WriteData), .Reg_Out(reg_32bit_18_reg_out));
  Reg_32Bit reg_32bit_19 (.CLK(and_19_out), .Reg_Input(WriteData), .Reg_Out(reg_32bit_19_reg_out));
  Reg_32Bit reg_32bit_20 (.CLK(and_20_out), .Reg_Input(WriteData), .Reg_Out(reg_32bit_20_reg_out));
  Reg_32Bit reg_32bit_21 (.CLK(and_21_out), .Reg_Input(WriteData), .Reg_Out(reg_32bit_21_reg_out));
  Reg_32Bit reg_32bit_22 (.CLK(and_22_out), .Reg_Input(WriteData), .Reg_Out(reg_32bit_22_reg_out));
  Reg_32Bit reg_32bit_23 (.CLK(and_23_out), .Reg_Input(WriteData), .Reg_Out(reg_32bit_23_reg_out));
  Reg_32Bit reg_32bit_24 (.CLK(and_24_out), .Reg_Input(WriteData), .Reg_Out(reg_32bit_24_reg_out));
  Reg_32Bit reg_32bit_25 (.CLK(and_25_out), .Reg_Input(WriteData), .Reg_Out(reg_32bit_25_reg_out));
  Reg_32Bit reg_32bit_26 (.CLK(and_26_out), .Reg_Input(WriteData), .Reg_Out(reg_32bit_26_reg_out));
  Reg_32Bit reg_32bit_27 (.CLK(and_27_out), .Reg_Input(WriteData), .Reg_Out(reg_32bit_27_reg_out));
  Reg_32Bit reg_32bit_28 (.CLK(and_28_out), .Reg_Input(WriteData), .Reg_Out(reg_32bit_28_reg_out));
  Reg_32Bit reg_32bit_29 (.CLK(and_29_out), .Reg_Input(WriteData), .Reg_Out(reg_32bit_29_reg_out));
  Reg_32Bit reg_32bit_30 (.CLK(and_30_out), .Reg_Input(WriteData), .Reg_Out(reg_32bit_30_reg_out));
  Reg_32Bit reg_32bit_31 (.CLK(and_31_out), .Reg_Input(WriteData), .Reg_Out(reg_32bit_31_reg_out));
  Multiplexer #(.select(5), .width(32)) multiplexer_1 (
    .in0({32{1'b0}}), .in1(reg_32bit_1_reg_out), .in2(reg_32bit_2_reg_out), .in3(reg_32bit_3_reg_out),
    .in4(reg_32bit_4_reg_out), .in5(reg_32bit_5_reg_out), .in6(reg_32bit_6_reg_out),
    .in7(reg_32bit_7_reg_out), .in8(reg_32bit_8_reg_out), .in9(reg_32bit_9_reg_out),
    .in10(reg_32bit_10_reg_out), .in11(reg_32bit_11_reg_out), .in12(reg_32bit_12_reg_out),
    .in13(reg_32bit_13_reg_out), .in14(reg_32bit_14_reg_out), .in15(reg_32bit_15_reg_out),
    .in16(reg_32bit_16_reg_out), .in17(reg_32bit_17_reg_out), .in18(reg_32bit_18_reg_out),
    .in19(reg_32bit_19_reg_out), .in20(reg_32bit_20_reg_out), .in21(reg_32bit_21_reg_out),
    .in22(reg_32bit_22_reg_out), .in23(reg_32bit_23_reg_out), .in24(reg_32bit_24_reg_out),
    .in25(reg_32bit_25_reg_out), .in26(reg_32bit_26_reg_out), .in27(reg_32bit_27_reg_out),
    .in28(reg_32bit_28_reg_out), .in29(reg_32bit_29_reg_out), .in30(reg_32bit_30_reg_out),
    .in31(reg_32bit_31_reg_out), .out(Output_1), .sel(Read_Reg_1));
  Multiplexer #(.select(5), .width(32)) multiplexer_2 (
    .in0({32{1'b0}}), .in1(reg_32bit_1_reg_out), .in2(reg_32bit_2_reg_out), .in3(reg_32bit_3_reg_out),
    .in4(reg_32bit_4_reg_out), .in5(reg_32bit_5_reg_out), .in6(reg_32bit_6_reg_out),
    .in7(reg_32bit_7_reg_out), .in8(reg_32bit_8_reg_out), .in9(reg_32bit_9_reg_out),
    .in10(reg_32bit_10_reg_out), .in11(reg_32bit_11_reg_out), .in12(reg_32bit_12_reg_out),
    .in13(reg_32bit_13_reg_out), .in14(reg_32bit_14_reg_out), .in15(reg_32bit_15_reg_out),
    .in16(reg_32bit_16_reg_out), .in17(reg_32bit_17_reg_out), .in18(reg_32bit_18_reg_out),
    .in19(reg_32bit_19_reg_out), .in20(reg_32bit_20_reg_out), .in21(reg_32bit_21_reg_out),
    .in22(reg_32bit_22_reg_out), .in23(reg_32bit_23_reg_out), .in24(reg_32bit_24_reg_out),
    .in25(reg_32bit_25_reg_out), .in26(reg_32bit_26_reg_out), .in27(reg_32bit_27_reg_out),
    .in28(reg_32bit_28_reg_out), .in29(reg_32bit_29_reg_out), .in30(reg_32bit_30_reg_out),
    .in31(reg_32bit_31_reg_out), .out(Output_2), .sel(Read_Reg_2));
endmodule

module Reg_32Bit (
  input  CLK,
  input  [31:0] Reg_Input,
  output [31:0] Reg_Out
);

  D_Flip_Flop d_ff_1 (.D(Reg_Input[31]), .clk(CLK), .Q(Reg_Out[31]), .preset(1'b0), .reset(1'b0));  // open: Qn
  D_Flip_Flop d_ff_2 (.D(Reg_Input[15]), .clk(CLK), .Q(Reg_Out[15]), .preset(1'b0), .reset(1'b0));  // open: Qn
  D_Flip_Flop d_ff_3 (.D(Reg_Input[30]), .clk(CLK), .Q(Reg_Out[30]), .preset(1'b0), .reset(1'b0));  // open: Qn
  D_Flip_Flop d_ff_4 (.D(Reg_Input[14]), .clk(CLK), .Q(Reg_Out[14]), .preset(1'b0), .reset(1'b0));  // open: Qn
  D_Flip_Flop d_ff_5 (.D(Reg_Input[29]), .clk(CLK), .Q(Reg_Out[29]), .preset(1'b0), .reset(1'b0));  // open: Qn
  D_Flip_Flop d_ff_6 (.D(Reg_Input[13]), .clk(CLK), .Q(Reg_Out[13]), .preset(1'b0), .reset(1'b0));  // open: Qn
  D_Flip_Flop d_ff_7 (.D(Reg_Input[28]), .clk(CLK), .Q(Reg_Out[28]), .preset(1'b0), .reset(1'b0));  // open: Qn
  D_Flip_Flop d_ff_8 (.D(Reg_Input[12]), .clk(CLK), .Q(Reg_Out[12]), .preset(1'b0), .reset(1'b0));  // open: Qn
  D_Flip_Flop d_ff_9 (.D(Reg_Input[27]), .clk(CLK), .Q(Reg_Out[27]), .preset(1'b0), .reset(1'b0));  // open: Qn
  D_Flip_Flop d_ff_10 (.D(Reg_Input[11]), .clk(CLK), .Q(Reg_Out[11]), .preset(1'b0), .reset(1'b0));  // open: Qn
  D_Flip_Flop d_ff_11 (.D(Reg_Input[26]), .clk(CLK), .Q(Reg_Out[26]), .preset(1'b0), .reset(1'b0));  // open: Qn
  D_Flip_Flop d_ff_12 (.D(Reg_Input[10]), .clk(CLK), .Q(Reg_Out[10]), .preset(1'b0), .reset(1'b0));  // open: Qn
  D_Flip_Flop d_ff_13 (.D(Reg_Input[25]), .clk(CLK), .Q(Reg_Out[25]), .preset(1'b0), .reset(1'b0));  // open: Qn
  D_Flip_Flop d_ff_14 (.D(Reg_Input[9]), .clk(CLK), .Q(Reg_Out[9]), .preset(1'b0), .reset(1'b0));  // open: Qn
  D_Flip_Flop d_ff_15 (.D(Reg_Input[24]), .clk(CLK), .Q(Reg_Out[24]), .preset(1'b0), .reset(1'b0));  // open: Qn
  D_Flip_Flop d_ff_16 (.D(Reg_Input[8]), .clk(CLK), .Q(Reg_Out[8]), .preset(1'b0), .reset(1'b0));  // open: Qn
  D_Flip_Flop d_ff_17 (.D(Reg_Input[23]), .clk(CLK), .Q(Reg_Out[23]), .preset(1'b0), .reset(1'b0));  // open: Qn
  D_Flip_Flop d_ff_18 (.D(Reg_Input[7]), .clk(CLK), .Q(Reg_Out[7]), .preset(1'b0), .reset(1'b0));  // open: Qn
  D_Flip_Flop d_ff_19 (.D(Reg_Input[22]), .clk(CLK), .Q(Reg_Out[22]), .preset(1'b0), .reset(1'b0));  // open: Qn
  D_Flip_Flop d_ff_20 (.D(Reg_Input[6]), .clk(CLK), .Q(Reg_Out[6]), .preset(1'b0), .reset(1'b0));  // open: Qn
  D_Flip_Flop d_ff_21 (.D(Reg_Input[21]), .clk(CLK), .Q(Reg_Out[21]), .preset(1'b0), .reset(1'b0));  // open: Qn
  D_Flip_Flop d_ff_22 (.D(Reg_Input[5]), .clk(CLK), .Q(Reg_Out[5]), .preset(1'b0), .reset(1'b0));  // open: Qn
  D_Flip_Flop d_ff_23 (.D(Reg_Input[20]), .clk(CLK), .Q(Reg_Out[20]), .preset(1'b0), .reset(1'b0));  // open: Qn
  D_Flip_Flop d_ff_24 (.D(Reg_Input[4]), .clk(CLK), .Q(Reg_Out[4]), .preset(1'b0), .reset(1'b0));  // open: Qn
  D_Flip_Flop d_ff_25 (.D(Reg_Input[19]), .clk(CLK), .Q(Reg_Out[19]), .preset(1'b0), .reset(1'b0));  // open: Qn
  D_Flip_Flop d_ff_26 (.D(Reg_Input[3]), .clk(CLK), .Q(Reg_Out[3]), .preset(1'b0), .reset(1'b0));  // open: Qn
  D_Flip_Flop d_ff_27 (.D(Reg_Input[18]), .clk(CLK), .Q(Reg_Out[18]), .preset(1'b0), .reset(1'b0));  // open: Qn
  D_Flip_Flop d_ff_28 (.D(Reg_Input[2]), .clk(CLK), .Q(Reg_Out[2]), .preset(1'b0), .reset(1'b0));  // open: Qn
  D_Flip_Flop d_ff_29 (.D(Reg_Input[17]), .clk(CLK), .Q(Reg_Out[17]), .preset(1'b0), .reset(1'b0));  // open: Qn
  D_Flip_Flop d_ff_30 (.D(Reg_Input[1]), .clk(CLK), .Q(Reg_Out[1]), .preset(1'b0), .reset(1'b0));  // open: Qn
  D_Flip_Flop d_ff_31 (.D(Reg_Input[16]), .clk(CLK), .Q(Reg_Out[16]), .preset(1'b0), .reset(1'b0));  // open: Qn
  D_Flip_Flop d_ff_32 (.D(Reg_Input[0]), .clk(CLK), .Q(Reg_Out[0]), .preset(1'b0), .reset(1'b0));  // open: Qn
endmodule
