// Logisim project mips32B_NoJump.circ as structural Verilog: 8 circuits, main circuit main
module main (
  input  EnBtn
);

  wire alu_1_zero, and_1_out, and_2_out, CLK_out, multiplexer_1_out, nand_1_out, Reset_out;
  wire [3:0] rom_3_data;
  wire [4:0] multiplexer_2_out;
  wire [7:0] rom_1_p2, rom_1_p3, rom_2_data;
  wire [8:2] rom_2_data_2;
  wire [31:0] adder_1_out, adder_2_out, alu_1_result, multiplexer_3_out, multiplexer_4_out,
       multiplexer_5_out, ram_1_dout, regfile_1_output_1, regfile_1_output_2, register_1_q, shifter_1_out;
  wire [31:6] rom_1_p5;

  and and_1 (and_1_out, CLK_out, nand_1_out);
  Clock CLK (.out(CLK_out));
  Button Reset (.out(Reset_out));
  Adder #(.width(32)) adder_1 (.a(register_1_q), .b(32'h4), .out(adder_1_out), .cin(1'b0));  // open: cout
  Register #(.width(32)) register_1 (
    .D(multiplexer_4_out), .en(EnBtn), .clk(and_1_out), .Q(register_1_q), .clr(multiplexer_1_out));
  Multiplexer multiplexer_1 (.in0(register_1_q[24]), .in1(1'b1), .out(multiplexer_1_out), .sel(Reset_out));
  // ROM #(.addrWidth(24), .line("quad")) rom_1: pin names not known; wires that end beside it: register_1_q[23:0], rom_1_p2, rom_1_p3, {rom_1_p5[31], rom_1_p5[14:8]}, {rom_1_p5[7:6], rom_2_data[5:0]}
  nand nand_1 (nand_1_out, rom_2_data[0], rom_2_data[1], rom_2_data[2], rom_2_data[3], rom_2_data[4], rom_2_data[5], rom_1_p5[6], rom_1_p5[7], rom_1_p5[8], rom_1_p5[9], rom_1_p5[10], rom_1_p5[11], rom_1_p5[12], rom_1_p5[13], rom_1_p5[14], rom_1_p5[31], rom_1_p3[1], rom_1_p3[2], rom_1_p3[3], rom_1_p3[4], rom_1_p3[5], rom_1_p3[6], rom_1_p3[7], rom_1_p2[0], rom_1_p2[1], rom_1_p2[2], rom_1_p2[3], rom_1_p2[4], rom_1_p2[5], rom_1_p2[6], rom_1_p2[7], rom_1_p3[0]);
  Multiplexer #(.width(5)) multiplexer_2 (
    .in0(rom_1_p3[4:0]), .in1({rom_1_p5[31], rom_1_p5[14:11]}), .out(multiplexer_2_out), .sel(rom_2_data_2[8]));
  ROM #(.addrWidth(6), .dataWidth(9)) rom_2 (.addr(rom_1_p2[7:2]), .data({rom_2_data_2, rom_2_data[7:6]}));
  ROM #(.dataWidth(4)) rom_3 (.addr(rom_2_data), .data(rom_3_data));
  RegFile regfile_1 (
    .WriteData(multiplexer_5_out), .CLK(and_1_out), .RST(multiplexer_1_out), .RegWrite(rom_2_data_2[5]),
    .WriteReg(multiplexer_2_out), .Read_Reg_1({rom_1_p2[1:0], rom_1_p3[7:5]}), .Read_Reg_2(rom_1_p3[4:0]),
    .Output_1(regfile_1_output_1), .Output_2(regfile_1_output_2));
  Multiplexer #(.width(32)) multiplexer_3 (
    .in0(regfile_1_output_2), .in1({{17{rom_1_p5[31]}}, rom_1_p5[14:6], rom_2_data[5:0]}),
    .out(multiplexer_3_out), .sel(rom_2_data_2[7]));
  Shifter #(.width(32)) shifter_1 (
    .in({{17{rom_1_p5[31]}}, rom_1_p5[14:6], rom_2_data[5:0]}), .\dist (5'b00010), .out(shifter_1_out));
  Multiplexer #(.width(32)) multiplexer_4 (
    .in0(adder_1_out), .in1(adder_2_out), .out(multiplexer_4_out), .sel(and_2_out));
  Adder #(.width(32)) adder_2 (.a(adder_1_out), .b(shifter_1_out), .out(adder_2_out), .cin(1'b0));  // open: cout
  and and_2 (and_2_out, rom_2_data_2[2], alu_1_zero);
  ALU alu_1 (
    .AInvert(rom_3_data[3]), .Bnegate(rom_3_data[2]), .OPR(rom_3_data[1:0]), .A(regfile_1_output_1),
    .B(multiplexer_3_out), .Result(alu_1_result), .Zero(alu_1_zero));  // open: OV_FLAG, Set_Flag, Cout
  RAM #(.addrWidth(24), .asyncread("true"), .clearpin("true"), .dataWidth(32)) ram_1 (
    .addr(alu_1_result[23:0]), .we(rom_2_data_2[3]), .oe(rom_2_data_2[4]), .clk(and_1_out),
    .din(regfile_1_output_2), .dout(ram_1_dout), .clr(multiplexer_1_out));
  Multiplexer #(.width(32)) multiplexer_5 (
    .in0(alu_1_result), .in1(ram_1_dout), .out(multiplexer_5_out), .sel(rom_2_data_2[6]));

  // Notes on the sheet:
  //   contents of rom_1 (hex, n*v repeats v):
  //   20 8 0 7 ac 8 0 0 20 8 0 3 ac 8 0 1 20 8 0 9 ac 8 0 2 20 8 0 1 ac 8 0 3 20 8 0 4 ac 8 0 4 20 8 0 8
  //   ac 8 0 5 20 8 0 2 ac 8 0 6 20 8 0 6 ac 8 0 7 20 9 0 0 20 b 0 0 20 d 0 8 8d 6c 0 0 1 2c 48 20 21 6b 0
  //   1 21 ad ff ff 20 0 0 0 11 a0 0 1 10 0 ff f9 ac 9 0 8 20 b 0 0 20 d 0 7 20 e 0 4 8d 69 0 0 8d aa 0 0
  //   ad 6a 0 0 ad a9 0 0 21 6b 0 1 21 ad ff ff 21 ce ff ff 20 0 0 0 11 c0 0 1 10 0 ff f6 20 9 0 0 20 b 0
  //   0 20 d 0 8 8d 6c 0 0 1 2c 48 20 21 6b 0 1 21 ad ff ff 20 0 0 0 11 a0 0 1 10 0 ff f9 ac 9 0 9 4*ff
  //   contents of rom_2 (hex, n*v repeats v):
  //   122 0 0 0 5 0 0 0 a0 26*0 f0 7*0 88
  //   contents of rom_3 (hex, n*v repeats v):
  //   64*2 64*6 2 0 6 0 0 1 4*0 7 5*0 2 0 6 0 0 1 4*0 7 5*0 2 0 6 0 0 1 4*0 7 5*0 2 0 6 0 0 1 4*0 7
  //   RegDst, alusrc, memtoreg, regWrite, memread, Memwrite, Branch, ALUOP1, ALUP0
endmodule

module RegFile (
  input  [31:0] WriteData,
  input  CLK,
  input  RST,
  input  RegWrite,
  input  [4:0] WriteReg,
  input  [4:0] Read_Reg_1,
  input  [4:0] Read_Reg_2,
  output [31:0] Output_1,
  output [31:0] Output_2
);

  wire decoder_1_out0, decoder_1_out1, decoder_1_out2, decoder_1_out3, decoder_1_out4, decoder_1_out5,
       decoder_1_out6, decoder_1_out7;
  wire [7:0] decoder_1_out8, decoder_1_out16, decoder_1_out24;
  wire [31:0] register_1_q, register_2_q, register_3_q, register_4_q, register_5_q, register_6_q,
       register_7_q, register_8_q, register_9_q, register_10_q, register_11_q, register_12_q, register_13_q,
       register_14_q, register_15_q, register_16_q, register_17_q, register_18_q, register_19_q,
       register_20_q, register_21_q, register_22_q, register_23_q, register_24_q, register_25_q,
       register_26_q, register_27_q, register_28_q, register_29_q, register_30_q, register_31_q,
       register_32_q;

  Decoder #(.select(5)) decoder_1 (
    .out0(decoder_1_out0), .out1(decoder_1_out1), .out2(decoder_1_out2), .out3(decoder_1_out3),
    .out4(decoder_1_out4), .out5(decoder_1_out5), .out6(decoder_1_out6), .out7(decoder_1_out7),
    .out8(decoder_1_out8[0]), .out9(decoder_1_out8[1]), .out10(decoder_1_out8[2]), .out11(decoder_1_out8[3]),
    .out12(decoder_1_out8[4]), .out13(decoder_1_out8[5]), .out14(decoder_1_out8[6]),
    .out15(decoder_1_out8[7]), .out16(decoder_1_out16[0]), .out17(decoder_1_out16[1]),
    .out18(decoder_1_out16[2]), .out19(decoder_1_out16[3]), .out20(decoder_1_out16[4]),
    .out21(decoder_1_out16[5]), .out22(decoder_1_out16[6]), .out23(decoder_1_out16[7]),
    .out24(decoder_1_out24[0]), .out25(decoder_1_out24[1]), .out26(decoder_1_out24[2]),
    .out27(decoder_1_out24[3]), .out28(decoder_1_out24[4]), .out29(decoder_1_out24[5]),
    .out30(decoder_1_out24[6]), .out31(decoder_1_out24[7]), .sel(WriteReg), .en(RegWrite));
  Register #(.width(32)) register_1 (.D(WriteData), .en(decoder_1_out0), .clk(CLK), .Q(register_1_q), .clr(RST));
  Register #(.width(32)) register_2 (.D(WriteData), .en(decoder_1_out1), .clk(CLK), .Q(register_2_q), .clr(RST));
  Register #(.width(32)) register_3 (.D(WriteData), .en(decoder_1_out2), .clk(CLK), .Q(register_3_q), .clr(RST));
  Register #(.width(32)) register_4 (.D(WriteData), .en(decoder_1_out3), .clk(CLK), .Q(register_4_q), .clr(RST));
  Register #(.width(32)) register_5 (.D(WriteData), .en(decoder_1_out4), .clk(CLK), .Q(register_5_q), .clr(RST));
  Register #(.width(32)) register_6 (.D(WriteData), .en(decoder_1_out5), .clk(CLK), .Q(register_6_q), .clr(RST));
  Register #(.width(32)) register_7 (.D(WriteData), .en(decoder_1_out6), .clk(CLK), .Q(register_7_q), .clr(RST));
  Register #(.width(32)) register_8 (.D(WriteData), .en(decoder_1_out7), .clk(CLK), .Q(register_8_q), .clr(RST));
  Register #(.width(32)) register_9 (.D(WriteData), .en(decoder_1_out8[0]), .clk(CLK), .Q(register_9_q), .clr(RST));
  Register #(.width(32)) register_10 (.D(WriteData), .en(decoder_1_out8[1]), .clk(CLK), .Q(register_10_q), .clr(RST));
  Register #(.width(32)) register_11 (.D(WriteData), .en(decoder_1_out8[2]), .clk(CLK), .Q(register_11_q), .clr(RST));
  Register #(.width(32)) register_12 (.D(WriteData), .en(decoder_1_out8[3]), .clk(CLK), .Q(register_12_q), .clr(RST));
  Register #(.width(32)) register_13 (.D(WriteData), .en(decoder_1_out8[4]), .clk(CLK), .Q(register_13_q), .clr(RST));
  Register #(.width(32)) register_14 (.D(WriteData), .en(decoder_1_out8[5]), .clk(CLK), .Q(register_14_q), .clr(RST));
  Register #(.width(32)) register_15 (.D(WriteData), .en(decoder_1_out8[6]), .clk(CLK), .Q(register_15_q), .clr(RST));
  Register #(.width(32)) register_16 (.D(WriteData), .en(decoder_1_out8[7]), .clk(CLK), .Q(register_16_q), .clr(RST));
  Register #(.width(32)) register_17 (.D(WriteData), .en(decoder_1_out16[0]), .clk(CLK), .Q(register_17_q), .clr(RST));
  Register #(.width(32)) register_18 (.D(WriteData), .en(decoder_1_out16[1]), .clk(CLK), .Q(register_18_q), .clr(RST));
  Register #(.width(32)) register_19 (.D(WriteData), .en(decoder_1_out16[2]), .clk(CLK), .Q(register_19_q), .clr(RST));
  Register #(.width(32)) register_20 (.D(WriteData), .en(decoder_1_out16[3]), .clk(CLK), .Q(register_20_q), .clr(RST));
  Register #(.width(32)) register_21 (.D(WriteData), .en(decoder_1_out16[4]), .clk(CLK), .Q(register_21_q), .clr(RST));
  Register #(.width(32)) register_22 (.D(WriteData), .en(decoder_1_out16[5]), .clk(CLK), .Q(register_22_q), .clr(RST));
  Register #(.width(32)) register_23 (.D(WriteData), .en(decoder_1_out16[6]), .clk(CLK), .Q(register_23_q), .clr(RST));
  Register #(.width(32)) register_24 (.D(WriteData), .en(decoder_1_out16[7]), .clk(CLK), .Q(register_24_q), .clr(RST));
  Register #(.width(32)) register_25 (.D(WriteData), .en(decoder_1_out24[0]), .clk(CLK), .Q(register_25_q), .clr(RST));
  Register #(.width(32)) register_26 (.D(WriteData), .en(decoder_1_out24[1]), .clk(CLK), .Q(register_26_q), .clr(RST));
  Register #(.width(32)) register_27 (.D(WriteData), .en(decoder_1_out24[2]), .clk(CLK), .Q(register_27_q), .clr(RST));
  Register #(.width(32)) register_28 (.D(WriteData), .en(decoder_1_out24[3]), .clk(CLK), .Q(register_28_q), .clr(RST));
  Register #(.width(32)) register_29 (.D(WriteData), .en(decoder_1_out24[4]), .clk(CLK), .Q(register_29_q), .clr(RST));
  Register #(.width(32)) register_30 (.D(WriteData), .en(decoder_1_out24[5]), .clk(CLK), .Q(register_30_q), .clr(RST));
  Register #(.width(32)) register_31 (.D(WriteData), .en(decoder_1_out24[6]), .clk(CLK), .Q(register_31_q), .clr(RST));
  Register #(.width(32)) register_32 (.D(WriteData), .en(decoder_1_out24[7]), .clk(CLK), .Q(register_32_q), .clr(RST));
  Multiplexer #(.select(5), .width(32)) multiplexer_1 (
    .in0(register_1_q), .in1(register_2_q), .in2(register_3_q), .in3(register_4_q), .in4(register_5_q),
    .in5(register_6_q), .in6(register_7_q), .in7(register_8_q), .in8(register_9_q), .in9(register_10_q),
    .in10(register_11_q), .in11(register_12_q), .in12(register_13_q), .in13(register_14_q),
    .in14(register_15_q), .in15(register_16_q), .in16(register_17_q), .in17(register_18_q),
    .in18(register_19_q), .in19(register_20_q), .in20(register_21_q), .in21(register_22_q),
    .in22(register_23_q), .in23(register_24_q), .in24(register_25_q), .in25(register_26_q),
    .in26(register_27_q), .in27(register_28_q), .in28(register_29_q), .in29(register_30_q),
    .in30(register_31_q), .in31(register_32_q), .out(Output_1), .sel(Read_Reg_1));
  Multiplexer #(.select(5), .width(32)) multiplexer_2 (
    .in0(register_1_q), .in1(register_2_q), .in2(register_3_q), .in3(register_4_q), .in4(register_5_q),
    .in5(register_6_q), .in6(register_7_q), .in7(register_8_q), .in8(register_9_q), .in9(register_10_q),
    .in10(register_11_q), .in11(register_12_q), .in12(register_13_q), .in13(register_14_q),
    .in14(register_15_q), .in15(register_16_q), .in16(register_17_q), .in17(register_18_q),
    .in18(register_19_q), .in19(register_20_q), .in20(register_21_q), .in21(register_22_q),
    .in22(register_23_q), .in23(register_24_q), .in24(register_25_q), .in25(register_26_q),
    .in26(register_27_q), .in27(register_28_q), .in28(register_29_q), .in29(register_30_q),
    .in30(register_31_q), .in31(register_32_q), .out(Output_2), .sel(Read_Reg_2));
endmodule

module CLA (
  input  G0,
  input  C0,
  input  G1,
  input  G2,
  input  G3,
  input  P0,
  input  P1,
  input  P2,
  input  P3,
  output C3,
  output C1,
  output Cout,
  output C2,
  output Pg,
  output Gg
);

  wire and_1_out, and_2_out, and_3_out, and_4_out, and_5_out, and_6_out, and_8_out;

  or or_1 (Cout, G3, and_1_out);
  and and_1 (and_1_out, C3, P3);
  or or_2 (C3, G2, and_2_out);
  or or_3 (Gg, G3, and_3_out, and_4_out, and_5_out);
  and and_2 (and_2_out, C2, P2);
  and and_3 (and_3_out, P3, G2);
  and and_4 (and_4_out, P2, P3, G1);
  and and_5 (and_5_out, P3, P2, P1, G0);
  or or_4 (C2, G1, and_6_out);
  and and_6 (and_6_out, C1, P1);
  and and_7 (Pg, P0, P1, P2, P3);
  or or_5 (C1, G0, and_8_out);
  and and_8 (and_8_out, C0, P0);
endmodule

module OV_Logic (
  input  A,
  input  B,
  input  Sub,
  input  R,
  output OV
);

  wire and_1_out, and_2_out, not_1_out, not_2_out, not_3_out, xor_1_out, xor_2_out;

  not not_1 (not_1_out, A);
  not not_2 (not_2_out, B);
  xor xor_1 (xor_1_out, not_2_out, Sub);
  xor xor_2 (xor_2_out, B, Sub);
  not not_3 (not_3_out, R);
  and and_1 (and_1_out, not_1_out, xor_1_out, R);
  and and_2 (and_2_out, A, xor_2_out, not_3_out);
  or or_1 (OV, and_1_out, 1'b0, and_2_out);
endmodule

module CLA_2 (
  input  G0,
  input  G1,
  input  C0,
  input  P1,
  input  P0,
  output C1,
  output Cout
);

  wire and_1_out, and_2_out;

  or or_1 (Cout, G1, and_1_out);
  and and_1 (and_1_out, C1, P1);
  or or_2 (C1, G0, and_2_out);
  and and_2 (and_2_out, C0, P0);
endmodule

module PFA (
  input  X,
  input  Y,
  input  Cin,
  output Sum,
  output Pi,
  output Cout,
  output Gi
);

  wire and_1_out;

  xor xor_1 (Pi, X, Y);
  and and_1 (and_1_out, Pi, Cin);
  and and_2 (Gi, X, Y);
  xor xor_2 (Sum, Pi, Cin);
  or or_1 (Cout, and_1_out, Gi);
endmodule

module ALU_4BIT (
  input  A3,
  input  A2,
  input  A1,
  input  A0,
  input  B3,
  input  B2,
  input  B1,
  input  B0,
  input  AInv,
  input  BInv,
  input  C0,
  input  Less,
  input  [1:0] OPR,
  output OV_FLAG,
  output Set_Flag,
  output S3,
  output S2,
  output S1,
  output S0,
  output Set,
  output c4,
  output Pg,
  output Gg
);

  wire and_1_out, and_2_out, and_3_out, and_4_out, cla_1_c1, cla_1_c2, cla_1_c3, multiplexer_1_out,
       multiplexer_2_out, multiplexer_4_out, multiplexer_5_out, multiplexer_7_out, multiplexer_8_out,
       multiplexer_10_out, multiplexer_11_out, not_1_out, not_2_out, not_3_out, not_4_out, not_5_out,
       not_6_out, not_7_out, not_8_out, or_1_out, or_2_out, or_3_out, or_4_out, ov_logic_2_ov, ov_logic_3_ov,
       ov_logic_4_ov, pfa_1_gi, pfa_1_pi, pfa_1_sum, pfa_2_cout, pfa_2_gi, pfa_2_pi, pfa_2_sum, pfa_3_cout,
       pfa_3_gi, pfa_3_pi, pfa_3_sum, pfa_4_cout, pfa_4_gi, pfa_4_pi, pfa_4_sum;

  not not_1 (not_1_out, A3);
  Multiplexer multiplexer_1 (.in0(A3), .in1(not_1_out), .out(multiplexer_1_out), .sel(AInv));
  not not_2 (not_2_out, B3);
  Multiplexer multiplexer_2 (.in0(B3), .in1(not_2_out), .out(multiplexer_2_out), .sel(BInv));
  OV_Logic ov_logic_1 (.A(multiplexer_1_out), .B(multiplexer_2_out), .Sub(BInv), .R(pfa_1_sum), .OV(OV_FLAG));
  and and_1 (and_1_out, multiplexer_1_out, multiplexer_2_out);
  or or_1 (or_1_out, multiplexer_1_out, multiplexer_2_out);
  PFA pfa_1 (
    .X(multiplexer_1_out), .Y(multiplexer_2_out), .Cin(cla_1_c3), .Sum(pfa_1_sum), .Pi(pfa_1_pi), .Cout(Set),
    .Gi(pfa_1_gi));
  Multiplexer #(.select(2)) multiplexer_3 (
    .in0(and_1_out), .in1(or_1_out), .in2(pfa_1_sum), .in3(1'b0), .out(S3), .sel(OPR));
  not not_3 (not_3_out, A2);
  Multiplexer multiplexer_4 (.in0(A2), .in1(not_3_out), .out(multiplexer_4_out), .sel(AInv));
  not not_4 (not_4_out, B2);
  Multiplexer multiplexer_5 (.in0(B2), .in1(not_4_out), .out(multiplexer_5_out), .sel(BInv));
  OV_Logic ov_logic_2 (.A(multiplexer_4_out), .B(multiplexer_5_out), .Sub(BInv), .R(pfa_2_sum), .OV(ov_logic_2_ov));
  and and_2 (and_2_out, multiplexer_4_out, multiplexer_5_out);
  or or_2 (or_2_out, multiplexer_4_out, multiplexer_5_out);
  PFA pfa_2 (
    .X(multiplexer_4_out), .Y(multiplexer_5_out), .Cin(cla_1_c2), .Sum(pfa_2_sum), .Pi(pfa_2_pi),
    .Cout(pfa_2_cout), .Gi(pfa_2_gi));
  Multiplexer #(.select(2)) multiplexer_6 (
    .in0(and_2_out), .in1(or_2_out), .in2(pfa_2_sum), .in3(1'b0), .out(S2), .sel(OPR));
  CLA cla_1 (
    .G0(pfa_4_gi), .C0(C0), .G1(pfa_3_gi), .G2(pfa_2_gi), .G3(pfa_1_gi), .P0(pfa_4_pi), .P1(pfa_3_pi),
    .P2(pfa_2_pi), .P3(pfa_1_pi), .C3(cla_1_c3), .C1(cla_1_c1), .Cout(c4), .C2(cla_1_c2), .Pg(Pg), .Gg(Gg));
  not not_5 (not_5_out, A1);
  not not_6 (not_6_out, B1);
  Multiplexer multiplexer_7 (.in0(A1), .in1(not_5_out), .out(multiplexer_7_out), .sel(AInv));
  Multiplexer multiplexer_8 (.in0(B1), .in1(not_6_out), .out(multiplexer_8_out), .sel(BInv));
  and and_3 (and_3_out, multiplexer_7_out, multiplexer_8_out);
  or or_3 (or_3_out, multiplexer_7_out, multiplexer_8_out);
  PFA pfa_3 (
    .X(multiplexer_7_out), .Y(multiplexer_8_out), .Cin(cla_1_c1), .Sum(pfa_3_sum), .Pi(pfa_3_pi),
    .Cout(pfa_3_cout), .Gi(pfa_3_gi));
  OV_Logic ov_logic_3 (.A(multiplexer_7_out), .B(multiplexer_8_out), .Sub(BInv), .R(pfa_3_sum), .OV(ov_logic_3_ov));
  Multiplexer #(.select(2)) multiplexer_9 (
    .in0(and_3_out), .in1(or_3_out), .in2(pfa_3_sum), .in3(1'b0), .out(S1), .sel(OPR));
  not not_7 (not_7_out, A0);
  not not_8 (not_8_out, B0);
  Multiplexer multiplexer_10 (.in0(A0), .in1(not_7_out), .out(multiplexer_10_out), .sel(AInv));
  Multiplexer multiplexer_11 (.in0(B0), .in1(not_8_out), .out(multiplexer_11_out), .sel(BInv));
  OV_Logic ov_logic_4 (.A(multiplexer_10_out), .B(multiplexer_11_out), .Sub(BInv), .R(pfa_4_sum), .OV(ov_logic_4_ov));
  and and_4 (and_4_out, multiplexer_10_out, multiplexer_11_out);
  or or_4 (or_4_out, multiplexer_10_out, multiplexer_11_out);
  PFA pfa_4 (
    .X(multiplexer_10_out), .Y(multiplexer_11_out), .Cin(C0), .Sum(pfa_4_sum), .Pi(pfa_4_pi),
    .Cout(pfa_4_cout), .Gi(pfa_4_gi));
  Multiplexer #(.select(2)) multiplexer_12 (
    .in0(and_4_out), .in1(or_4_out), .in2(pfa_4_sum), .in3(Less), .out(S0), .sel(OPR));

  assign Set_Flag = Set;
endmodule

module ALU (
  input  AInvert,
  input  Bnegate,
  input  [1:0] OPR,
  input  [31:0] A,
  input  [31:0] B,
  output OV_FLAG,
  output Set_Flag,
  output Cout,
  output [31:0] Result,
  output Zero
);

  wire alu_4bit_1_gg, alu_4bit_1_pg, alu_4bit_1_set, alu_4bit_2_c4, alu_4bit_2_gg, alu_4bit_2_pg,
       alu_4bit_2_set, alu_4bit_3_c4, alu_4bit_3_gg, alu_4bit_3_pg, alu_4bit_3_set, alu_4bit_4_c4,
       alu_4bit_4_gg, alu_4bit_4_pg, alu_4bit_4_set, alu_4bit_5_c4, alu_4bit_5_gg, alu_4bit_5_pg,
       alu_4bit_5_set, alu_4bit_6_c4, alu_4bit_6_gg, alu_4bit_6_pg, alu_4bit_6_set, alu_4bit_7_c4,
       alu_4bit_7_gg, alu_4bit_7_pg, alu_4bit_7_set, alu_4bit_8_c4, alu_4bit_8_gg, alu_4bit_8_pg, cla_1_c1,
       cla_1_c2, cla_1_c3, cla_1_cout, cla_1_gg, cla_1_pg, cla_2_c1, cla_2_c2, cla_2_c3, cla_2_cout,
       cla_2_gg, cla_2_pg;

  nor nor_1 (Zero, Result[0], Result[1], Result[2], Result[3], Result[4], Result[5], Result[6], Result[7], Result[8], Result[9], Result[10], Result[11], Result[12], Result[13], Result[14], Result[15], Result[17], Result[18], Result[19], Result[20], Result[21], Result[22], Result[23], Result[24], Result[25], Result[26], Result[27], Result[28], Result[29], Result[30], Result[31], Result[16]);
  ALU_4BIT alu_4bit_1 (
    .A3(A[31]), .A2(A[30]), .A1(A[29]), .A0(A[28]), .B3(B[31]), .B2(B[30]), .B1(B[29]), .B0(B[28]),
    .AInv(AInvert), .BInv(Bnegate), .C0(cla_1_c3), .Less(1'b0), .OPR(OPR), .OV_FLAG(OV_FLAG),
    .Set_Flag(Set_Flag), .S3(Result[31]), .S2(Result[30]), .S1(Result[29]), .S0(Result[28]),
    .Set(alu_4bit_1_set), .c4(Cout), .Pg(alu_4bit_1_pg), .Gg(alu_4bit_1_gg));
  ALU_4BIT alu_4bit_2 (
    .A3(A[15]), .A2(A[14]), .A1(A[13]), .A0(A[12]), .B3(B[15]), .B2(B[14]), .B1(B[13]), .B0(B[12]),
    .AInv(AInvert), .BInv(Bnegate), .C0(cla_2_c3), .Less(1'b0), .OPR(OPR), .S3(Result[15]), .S2(Result[14]),
    .S1(Result[13]), .S0(Result[12]), .Set(alu_4bit_2_set), .c4(alu_4bit_2_c4), .Pg(alu_4bit_2_pg),
    .Gg(alu_4bit_2_gg));  // open: OV_FLAG, Set_Flag
  ALU_4BIT alu_4bit_3 (
    .A3(A[27]), .A2(A[26]), .A1(A[25]), .A0(A[24]), .B3(B[27]), .B2(B[26]), .B1(B[25]), .B0(B[24]),
    .AInv(AInvert), .BInv(Bnegate), .C0(cla_1_c2), .Less(1'b0), .OPR(OPR), .S3(Result[27]), .S2(Result[26]),
    .S1(Result[25]), .S0(Result[24]), .Set(alu_4bit_3_set), .c4(alu_4bit_3_c4), .Pg(alu_4bit_3_pg),
    .Gg(alu_4bit_3_gg));  // open: OV_FLAG, Set_Flag
  ALU_4BIT alu_4bit_4 (
    .A3(A[11]), .A2(A[10]), .A1(A[9]), .A0(A[8]), .B3(B[11]), .B2(B[10]), .B1(B[9]), .B0(B[8]),
    .AInv(AInvert), .BInv(Bnegate), .C0(cla_2_c2), .Less(1'b0), .OPR(OPR), .S3(Result[11]), .S2(Result[10]),
    .S1(Result[9]), .S0(Result[8]), .Set(alu_4bit_4_set), .c4(alu_4bit_4_c4), .Pg(alu_4bit_4_pg),
    .Gg(alu_4bit_4_gg));  // open: OV_FLAG, Set_Flag
  CLA cla_1 (
    .G0(alu_4bit_7_gg), .C0(cla_2_cout), .G1(alu_4bit_5_gg), .G2(alu_4bit_3_gg), .G3(alu_4bit_1_gg),
    .P0(alu_4bit_7_pg), .P1(alu_4bit_5_pg), .P2(alu_4bit_3_pg), .P3(alu_4bit_1_pg), .C3(cla_1_c3),
    .C1(cla_1_c1), .Cout(cla_1_cout), .C2(cla_1_c2), .Pg(cla_1_pg), .Gg(cla_1_gg));
  CLA cla_2 (
    .G0(alu_4bit_8_gg), .C0(Bnegate), .G1(alu_4bit_6_gg), .G2(alu_4bit_4_gg), .G3(alu_4bit_2_gg),
    .P0(alu_4bit_8_pg), .P1(alu_4bit_6_pg), .P2(alu_4bit_4_pg), .P3(alu_4bit_2_pg), .C3(cla_2_c3),
    .C1(cla_2_c1), .Cout(cla_2_cout), .C2(cla_2_c2), .Pg(cla_2_pg), .Gg(cla_2_gg));
  ALU_4BIT alu_4bit_5 (
    .A3(A[23]), .A2(A[22]), .A1(A[21]), .A0(A[20]), .B3(B[23]), .B2(B[22]), .B1(B[21]), .B0(B[20]),
    .AInv(AInvert), .BInv(Bnegate), .C0(cla_1_c1), .Less(1'b0), .OPR(OPR), .S3(Result[23]), .S2(Result[22]),
    .S1(Result[21]), .S0(Result[20]), .Set(alu_4bit_5_set), .c4(alu_4bit_5_c4), .Pg(alu_4bit_5_pg),
    .Gg(alu_4bit_5_gg));  // open: OV_FLAG, Set_Flag
  ALU_4BIT alu_4bit_6 (
    .A3(A[7]), .A2(A[6]), .A1(A[5]), .A0(A[4]), .B3(B[7]), .B2(B[6]), .B1(B[5]), .B0(B[4]), .AInv(AInvert),
    .BInv(Bnegate), .C0(cla_2_c1), .Less(1'b0), .OPR(OPR), .S3(Result[7]), .S2(Result[6]), .S1(Result[5]),
    .S0(Result[4]), .Set(alu_4bit_6_set), .c4(alu_4bit_6_c4), .Pg(alu_4bit_6_pg), .Gg(alu_4bit_6_gg));  // open: OV_FLAG, Set_Flag
  ALU_4BIT alu_4bit_7 (
    .A3(A[19]), .A2(A[18]), .A1(A[17]), .A0(A[16]), .B3(B[19]), .B2(B[18]), .B1(B[17]), .B0(B[16]),
    .AInv(AInvert), .BInv(Bnegate), .C0(cla_2_cout), .Less(1'b0), .OPR(OPR), .S3(Result[19]),
    .S2(Result[18]), .S1(Result[17]), .S0(Result[16]), .Set(alu_4bit_7_set), .c4(alu_4bit_7_c4),
    .Pg(alu_4bit_7_pg), .Gg(alu_4bit_7_gg));  // open: OV_FLAG, Set_Flag
  ALU_4BIT alu_4bit_8 (
    .A3(A[3]), .A2(A[2]), .A1(A[1]), .A0(A[0]), .B3(B[3]), .B2(B[2]), .B1(B[1]), .B0(B[0]), .AInv(AInvert),
    .BInv(Bnegate), .C0(Bnegate), .Less(alu_4bit_1_set), .OPR(OPR), .S3(Result[3]), .S2(Result[2]),
    .S1(Result[1]), .S0(Result[0]), .c4(alu_4bit_8_c4), .Pg(alu_4bit_8_pg), .Gg(alu_4bit_8_gg));  // open: OV_FLAG, Set_Flag, Set
endmodule
