// Logisim project simpleProgramC.circ as structural Verilog: 1 circuit, main circuit main
module main (
  input  in_1,
  input  in_2,
  output [3:0] out_3
);

  wire and_1_out, clock_1_out;
  wire [3:0] adder_1_out;

  Clock clock_1 (.out(clock_1_out));
  and and_1 (and_1_out, in_1, clock_1_out);
  D_Flip_Flop d_ff_1 (.D(adder_1_out[3]), .clk(and_1_out), .Q(out_3[3]), .reset(in_2));  // open: Qn, preset
  D_Flip_Flop d_ff_2 (.D(adder_1_out[2]), .clk(and_1_out), .Q(out_3[2]), .reset(in_2));  // open: Qn, preset
  D_Flip_Flop d_ff_3 (.D(adder_1_out[1]), .clk(and_1_out), .Q(out_3[1]), .reset(in_2));  // open: Qn, preset
  D_Flip_Flop d_ff_4 (.D(adder_1_out[0]), .clk(and_1_out), .Q(out_3[0]), .reset(in_2));  // open: Qn, preset
  Adder #(.width(4)) adder_1 (.a(out_3), .b(4'b0010), .out(adder_1_out));  // open: cin, cout
endmodule
